// Logisim project cpu.circ as structural Verilog: 56 circuits, main circuit Computer
module Test (
  input  [3:0] in_1,
  input  [15:0] A,
  input  [15:0] B,
  input  [15:0] data_in,
  input  [31:0] address,
  input  [3:0] A_index,
  input  [3:0] B_index,
  input  [15:0] A_in,
  input  [31:0] write,
  input  clock,
  input  [15:0] Status_in
);

  wire button_1_out, button_2_out, comparator_16bit_premux_1_eq, comparator_16bit_premux_1_gt,
       comparator_16bit_premux_1_gte, comparator_16bit_premux_1_gteu, comparator_16bit_premux_1_gtu,
       comparator_16bit_premux_1_lt, comparator_16bit_premux_1_lte, comparator_16bit_premux_1_lteu,
       comparator_16bit_premux_1_ltu, comparator_16bit_premux_1_neq, or_1_out, or_2_out, or_3_out;
  wire [1:0] ram_1kb_with_controller_a_1_error;
  wire [3:0] alu_16bit_extended_1_status;
  wire [15:0] adder_1_out, alu_16bit_extended_1_result, register_file_16_1_a_out, register_file_16_1_b_out,
       register_file_16_1_pc_out, register_file_16_1_status_out, shifter_16bit_byn_1_data_out;
  wire [31:0] ram_1kb_with_controller_a_1_data_out;

  ALU_16bit_extended alu_16bit_extended_1 (
    .b(B), .a(A), .operation(3'b111), .result(alu_16bit_extended_1_result),
    .status(alu_16bit_extended_1_status));
  // Probe on alu_16bit_extended_1_result
  // Probe on adder_1_out
  // Probe on alu_16bit_extended_1_result
  // Probe on alu_16bit_extended_1_result
  Button button_1 (.out(button_1_out));
  or or_1 (or_1_out, 1'b0, button_1_out);
  Register_File_16 register_file_16_1 (
    .B_out(register_file_16_1_b_out), .clock(or_3_out), .PC_in(adder_1_out), .Status_in(Status_in),
    .write_a(or_1_out), .A_out(register_file_16_1_a_out), .A_in(A_in), .A_index(A_index), .B_index(B_index),
    .PC_out(register_file_16_1_pc_out), .Status_out(register_file_16_1_status_out));
  // Probe on alu_16bit_extended_1_status[0]
  // Probe on alu_16bit_extended_1_status[1]
  // Probe on alu_16bit_extended_1_status[2]
  // Probe on alu_16bit_extended_1_status[3]
  Button button_2 (.out(button_2_out));
  or or_2 (or_2_out, button_2_out, 1'b0);
  or or_3 (or_3_out, or_1_out, or_2_out);
  Adder #(.width(16)) adder_1 (.a(register_file_16_1_pc_out), .b(16'h4), .out(adder_1_out));  // open: cin, cout
  Comparator_16bit_premux comparator_16bit_premux_1 (
    .neq(comparator_16bit_premux_1_neq), .lt(comparator_16bit_premux_1_lt), .A(A),
    .lteu(comparator_16bit_premux_1_lteu), .B(B), .lte(comparator_16bit_premux_1_lte),
    .ltu(comparator_16bit_premux_1_ltu), .status(alu_16bit_extended_1_status),
    .gtu(comparator_16bit_premux_1_gtu), .gteu(comparator_16bit_premux_1_gteu),
    .eq(comparator_16bit_premux_1_eq), .gt(comparator_16bit_premux_1_gt), .gte(comparator_16bit_premux_1_gte));
  // Probe on register_file_16_1_a_out
  // Probe on register_file_16_1_b_out
  // Probe on register_file_16_1_pc_out
  // Probe on register_file_16_1_status_out
  // Probe on data_in
  // Probe on address
  RAM_1KB_with_controller_A ram_1kb_with_controller_a_1 (
    .error(ram_1kb_with_controller_a_1_error), .operation(3'b000), .clock(clock), .data_in(write),
    .address(address), .data_out(ram_1kb_with_controller_a_1_data_out));
  // Probe on in_1
  Shifter_16bit_byn shifter_16bit_byn_1 (
    .shamt(in_1), .data_out(shifter_16bit_byn_1_data_out), .data_in(data_in), .operation(3'b000));
  // Probe on shifter_16bit_byn_1_data_out
  // Probe on shifter_16bit_byn_1_data_out
  // Probe on ram_1kb_with_controller_a_1_data_out
  // Probe on ram_1kb_with_controller_a_1_error[0]
  // Probe on ram_1kb_with_controller_a_1_error[1]
  // Probe on shifter_16bit_byn_1_data_out

  // Notes on the sheet:
  //   Operation
  //   Signed Base10
  //   16-Bit ALU Test
  //   Base2
  //   Unsigned Base10
  //   16-Bit Register File Test
  //   clock_write
  //   overflow
  //   carry
  //   sign
  //   zero
  //   clock_read
  //   16-Bit Comparator Test
  //   Operation
  //   Shift Amount
  //   Signed Base10
  //   1KB RAM Test
  //   16-Bit Shifter Test
  //   Base2
  //   unaligned
  //   Operation
  //   Unsigned Base10
  //   out-of-range
endmodule

module Full_Adder (
  input  A,
  input  B,
  input  carry_in,
  output sum,
  output carry_out
);

  wire and_1_out, and_2_out, xor_1_out;

  xor xor_1 (xor_1_out, A, B);
  xor xor_2 (sum, xor_1_out, carry_in);
  and and_1 (and_1_out, xor_1_out, carry_in);
  and and_2 (and_2_out, B, A);
  or or_1 (carry_out, and_1_out, and_2_out);

  // Notes on the sheet:
  //   Full Adder
  //   sum = A XOR B XOR C
  //   carry_out = AB OR C(A XOR B)
endmodule

module ALU_1bit (
  input  carry_in,
  input  [1:0] operation,
  input  a,
  input  b,
  output result,
  output carry_out
);

  wire and_1_out, full_adder_1_sum, or_1_out, xor_1_out;

  and and_1 (and_1_out, a, b);
  or or_1 (or_1_out, a, b);
  xor xor_1 (xor_1_out, a, b);
  Full_Adder full_adder_1 (.carry_out(carry_out), .carry_in(carry_in), .A(a), .B(b), .sum(full_adder_1_sum));
  Multiplexer #(.select(2), .enable("false")) multiplexer_1 (
    .in0(and_1_out), .in1(or_1_out), .in2(xor_1_out), .in3(full_adder_1_sum), .out(result), .sel(operation));

  // Notes on the sheet:
  //   1-Bit ALU
  //   Supported Operations:
  //   operation
  //   - AND
  //   0x0
  //   - OR
  //   0x1
  //   - XOR
  //   0x2
  //   - ADD
  //   0x3
  //   AND
  //   OR
  //   XOR
  //   ADD
endmodule

module ALU_8bit (
  input  [7:0] b,
  input  [7:0] a,
  input  carry_in,
  input  [1:0] operation,
  output carry_out,
  output [7:0] result
);

  wire alu_1bit_1_carry_out, alu_1bit_2_carry_out, alu_1bit_3_carry_out, alu_1bit_4_carry_out,
       alu_1bit_5_carry_out, alu_1bit_6_carry_out, alu_1bit_7_carry_out;

  // Probe on b
  // Probe on a
  ALU_1bit alu_1bit_1 (
    .b(b[0]), .operation(operation), .a(a[0]), .result(result[0]), .carry_in(carry_in),
    .carry_out(alu_1bit_1_carry_out));
  ALU_1bit alu_1bit_2 (
    .b(b[1]), .operation(operation), .a(a[1]), .result(result[1]), .carry_in(alu_1bit_1_carry_out),
    .carry_out(alu_1bit_2_carry_out));
  ALU_1bit alu_1bit_3 (
    .b(b[2]), .operation(operation), .a(a[2]), .result(result[2]), .carry_in(alu_1bit_2_carry_out),
    .carry_out(alu_1bit_3_carry_out));
  ALU_1bit alu_1bit_4 (
    .b(b[3]), .operation(operation), .a(a[3]), .result(result[3]), .carry_in(alu_1bit_3_carry_out),
    .carry_out(alu_1bit_4_carry_out));
  ALU_1bit alu_1bit_5 (
    .b(b[4]), .operation(operation), .a(a[4]), .result(result[4]), .carry_in(alu_1bit_4_carry_out),
    .carry_out(alu_1bit_5_carry_out));
  ALU_1bit alu_1bit_6 (
    .b(b[5]), .operation(operation), .a(a[5]), .result(result[5]), .carry_in(alu_1bit_5_carry_out),
    .carry_out(alu_1bit_6_carry_out));
  ALU_1bit alu_1bit_7 (
    .b(b[6]), .operation(operation), .a(a[6]), .result(result[6]), .carry_in(alu_1bit_6_carry_out),
    .carry_out(alu_1bit_7_carry_out));
  ALU_1bit alu_1bit_8 (
    .b(b[7]), .operation(operation), .a(a[7]), .result(result[7]), .carry_in(alu_1bit_7_carry_out),
    .carry_out(carry_out));
  // Probe on operation
  // Probe on result

  // Notes on the sheet:
  //   8-Bit ALU
  //   Native Operations:
  //   operation
  //   - AND
  //   0x0
  //   0x1
  //   - OR
  //   - XOR
  //   0x2
  //   - ADD
  //   0x3
endmodule

module ALU_8bit_with_control (
  input  ab_invert,
  input  b_negate,
  input  [1:0] operation,
  input  [7:0] A,
  input  [7:0] B,
  input  result_invert,
  output carry_out,
  output sign,
  output zero,
  output [7:0] result
);

  wire or_1_out;
  wire [7:0] alu_8bit_1_result, multiplexer_1_out, multiplexer_2_out, not_1_out, not_2_out, not_3_out;

  // Probe on A
  // Probe on B
  Multiplexer #(.width(8), .enable("false")) multiplexer_1 (
    .in0(A), .in1(not_1_out), .out(multiplexer_1_out), .sel(ab_invert));
  assign not_1_out = ~A;  // NOT_Gate not_1, 8 bits wide
  Multiplexer #(.width(8), .enable("false")) multiplexer_2 (
    .in0(B), .in1(not_2_out), .out(multiplexer_2_out), .sel(or_1_out));
  assign not_2_out = ~B;  // NOT_Gate not_2, 8 bits wide
  or or_1 (or_1_out, ab_invert, b_negate);
  ALU_8bit alu_8bit_1 (
    .carry_out(carry_out), .carry_in(b_negate), .operation(operation), .a(multiplexer_1_out),
    .b(multiplexer_2_out), .result(alu_8bit_1_result));
  assign not_3_out = ~alu_8bit_1_result;  // NOT_Gate not_3, 8 bits wide
  Multiplexer #(.width(8), .enable("false")) multiplexer_3 (
    .in0(alu_8bit_1_result), .in1(not_3_out), .out(result), .sel(result_invert));
  // Probe on operation
  BitSelector bitselector_1 (.in(result), .out(sign), .sel(3'b111));
  Comparator comparator_1 (.a(result), .b({8{1'b0}}), .eq(zero));  // open: gt, lt
  // Probe on result

  // Notes on the sheet:
  //   Native Operations:
  //   operation
  //   - AND
  //   0x0
  //   0x1
  //   - OR
  //   - XOR
  //   0x2
  //   - ADD
  //   0x3
  //   8-Bit ALU with additional control inputs and status
  //   a_invert
  //   b_invert
endmodule

module ALU_8bit_extended (
  input  [7:0] a,
  input  [7:0] b,
  input  [2:0] in_3,
  output [7:0] result,
  output zero,
  output sign,
  output carry
);

  wire decoder_1_out0, decoder_1_out1, decoder_1_out2, decoder_1_out3, decoder_1_out4, decoder_1_out5,
       decoder_1_out6, decoder_1_out7, or_2_out, or_3_out, or_4_out, or_5_out, or_6_out;
  wire [1:0] multiplexer_1_out, multiplexer_2_out, multiplexer_3_out, multiplexer_4_out, or_1_out;

  // Probe on a
  // Probe on b
  ALU_8bit_with_control alu_8bit_with_control_1 (
    .B(b), .sign(sign), .result_invert(or_6_out), .carry_out(carry), .operation(or_1_out), .A(a),
    .b_negate(decoder_1_out7), .result(result), .zero(zero));  // open: ab_invert
  // Probe on result
  assign or_1_out = multiplexer_1_out | multiplexer_2_out | multiplexer_3_out | multiplexer_4_out;  // OR_Gate or_1, 2 bits wide
  Multiplexer #(.width(2)) multiplexer_1 (
    .in0(2'b00), .out(multiplexer_1_out), .sel(1'b0), .en(or_2_out));  // open: in1
  or or_2 (or_2_out, decoder_1_out0, decoder_1_out1);
  Multiplexer #(.width(2)) multiplexer_2 (
    .in0(2'b01), .out(multiplexer_2_out), .sel(1'b0), .en(or_3_out));  // open: in1
  or or_3 (or_3_out, decoder_1_out2, decoder_1_out3);
  Multiplexer #(.width(2)) multiplexer_3 (
    .in0(2'b10), .out(multiplexer_3_out), .sel(1'b0), .en(or_4_out));  // open: in1
  or or_4 (or_4_out, decoder_1_out4, decoder_1_out5);
  Multiplexer #(.width(2)) multiplexer_4 (
    .in0(2'b11), .out(multiplexer_4_out), .sel(1'b0), .en(or_5_out));  // open: in1
  or or_5 (or_5_out, decoder_1_out6, decoder_1_out7);
  or or_6 (or_6_out, decoder_1_out1, decoder_1_out3, decoder_1_out5);
  Decoder #(.select(3), .enable("false")) decoder_1 (
    .out0(decoder_1_out0), .out1(decoder_1_out1), .out2(decoder_1_out2), .out3(decoder_1_out3),
    .out4(decoder_1_out4), .out5(decoder_1_out5), .out6(decoder_1_out6), .out7(decoder_1_out7), .sel(in_3));
  // Probe on in_3

  // Notes on the sheet:
  //   Native Operations:
  //   operation
  //   - AND
  //   0x0
  //   - NAND
  //   0x1
  //   - OR
  //   0x2
  //   - NOR
  //   0x3
  //   - XOR
  //   0x4
  //   - XNOR
  //   0x5
  //   - ADD
  //   0x6
  //   - SUB
  //   0x7
  //   Non-Native Unary Operations:
  //   operation
  //   - NEG
  //   0x7
  //   - NOT
  //   0x3
  //   - INC
  //   0x6
  //   - DEC
  //   0x7
  //   Non-Native Comparison Operations:
  //   operation
  //   - EQ
  //   0x7
  //   - NEQ
  //   0x7
  //   - LT
  //   0x7
  //   - LTE
  //   0x7
  //   8-Bit Extended ALU
  //   b
  //   a
  //   num
  //   0
  //   num
  //   0
  //   num
  //   1
  //   1
  //   num
  //   true if
  //   zero
  //   NOT zero
  //   sign
  //   sign OR zero
  //   output as
  //   result
  //   result
  //   result
  //   result
  //   AND
  //   OR
  //   XOR
  //   ADD
  //   Chose basic ALU Operation
  //   result_invert
  //   b_negate
  //   <-
  //   AND
  //   NAND
  //   OR
  //   NOR
  //   XOR
  //   XNOR
  //   ADD
  //   SUB
  //   Chose extended ALU Operation
endmodule

module ALU_16bit (
  input  carry_in,
  input  [1:0] operation,
  input  [15:0] A,
  input  [15:0] B,
  output [15:0] result,
  output carry_out
);

  wire alu_8bit_1_carry_out;

  // Probe on A
  // Probe on B
  ALU_8bit alu_8bit_1 (
    .carry_out(alu_8bit_1_carry_out), .carry_in(carry_in), .operation(operation), .a(A[7:0]), .b(B[7:0]),
    .result(result[7:0]));
  ALU_8bit alu_8bit_2 (
    .carry_out(carry_out), .carry_in(alu_8bit_1_carry_out), .operation(operation), .a(A[15:8]), .b(B[15:8]),
    .result(result[15:8]));
  // Probe on result

  // Notes on the sheet:
  //   16-Bit ALU
  //   Native Operations:
  //   operation
  //   - AND
  //   0x0
  //   - OR
  //   0x1
  //   - XOR
  //   0x2
  //   - ADD
  //   0x3
endmodule

module ALU_16bit_with_control (
  input  b_negate,
  input  [15:0] A,
  input  [1:0] operation,
  input  [15:0] B,
  input  result_invert,
  output [15:0] result,
  output overflow,
  output carry_out,
  output sign,
  output zero
);

  wire [15:0] alu_16bit_1_result, multiplexer_1_out, not_1_out, not_2_out;

  // Probe on A
  // Probe on B
  Overflow_Detect_16bit overflow_detect_16bit_1 (.result(result), .overflow(overflow), .b(multiplexer_1_out), .a(A));
  Multiplexer #(.width(16), .enable("false")) multiplexer_1 (
    .in0(B), .in1(not_1_out), .out(multiplexer_1_out), .sel(b_negate));
  assign not_1_out = ~B;  // NOT_Gate not_1, 16 bits wide
  ALU_16bit alu_16bit_1 (
    .result(alu_16bit_1_result), .operation(operation), .carry_in(b_negate), .carry_out(carry_out), .A(A),
    .B(multiplexer_1_out));
  Multiplexer #(.width(16), .enable("false")) multiplexer_2 (
    .in0(alu_16bit_1_result), .in1(not_2_out), .out(result), .sel(result_invert));
  BitSelector #(.width(16)) bitselector_1 (.in(result), .out(sign), .sel(4'b1111));
  // Probe on operation
  assign not_2_out = ~alu_16bit_1_result;  // NOT_Gate not_2, 16 bits wide
  Comparator #(.width(16)) comparator_1 (.a(result), .b({16{1'b0}}), .eq(zero));  // open: gt, lt
  // Probe on result

  // Notes on the sheet:
  //   Native Operations:
  //   operation
  //   - AND
  //   0x0
  //   0x1
  //   - OR
  //   - XOR
  //   0x2
  //   - ADD
  //   0x3
  //   16-Bit ALU with additional control inputs and status
  //   b_invert
endmodule

module ALU_16bit_extended (
  input  [15:0] a,
  input  [15:0] b,
  input  [2:0] operation,
  output [15:0] result,
  output [3:0] status
);

  wire decoder_1_out0, decoder_1_out1, decoder_1_out2, decoder_1_out3, decoder_1_out4, decoder_1_out5,
       decoder_1_out6, decoder_1_out7, or_2_out, or_3_out, or_4_out, or_5_out, or_6_out;
  wire [1:0] multiplexer_1_out, multiplexer_2_out, multiplexer_3_out, multiplexer_4_out, or_1_out;

  // Probe on a
  // Probe on b
  ALU_16bit_with_control alu_16bit_with_control_1 (
    .operation(or_1_out), .b_negate(decoder_1_out7), .carry_out(status[1]), .A(a), .zero(status[3]),
    .result(result), .sign(status[2]), .B(b), .result_invert(or_6_out), .overflow(status[0]));
  // Probe on result
  assign or_1_out = multiplexer_1_out | multiplexer_2_out | multiplexer_3_out | multiplexer_4_out;  // OR_Gate or_1, 2 bits wide
  Multiplexer #(.width(2)) multiplexer_1 (
    .in0(2'b00), .out(multiplexer_1_out), .sel(1'b0), .en(or_2_out));  // open: in1
  or or_2 (or_2_out, decoder_1_out0, decoder_1_out1);
  Multiplexer #(.width(2)) multiplexer_2 (
    .in0(2'b01), .out(multiplexer_2_out), .sel(1'b0), .en(or_3_out));  // open: in1
  or or_3 (or_3_out, decoder_1_out2, decoder_1_out3);
  Multiplexer #(.width(2)) multiplexer_3 (
    .in0(2'b10), .out(multiplexer_3_out), .sel(1'b0), .en(or_4_out));  // open: in1
  or or_4 (or_4_out, decoder_1_out4, decoder_1_out5);
  Multiplexer #(.width(2)) multiplexer_4 (
    .in0(2'b11), .out(multiplexer_4_out), .sel(1'b0), .en(or_5_out));  // open: in1
  or or_5 (or_5_out, decoder_1_out6, decoder_1_out7);
  or or_6 (or_6_out, decoder_1_out1, decoder_1_out3, decoder_1_out5);
  Decoder #(.select(3), .enable("false")) decoder_1 (
    .out0(decoder_1_out0), .out1(decoder_1_out1), .out2(decoder_1_out2), .out3(decoder_1_out3),
    .out4(decoder_1_out4), .out5(decoder_1_out5), .out6(decoder_1_out6), .out7(decoder_1_out7),
    .sel(operation));
  // Probe on operation

  // Notes on the sheet:
  //   Native Operations:
  //   operation
  //   - AND
  //   0x0
  //   - NAND
  //   0x1
  //   - OR
  //   0x2
  //   - NOR
  //   0x3
  //   - XOR
  //   0x4
  //   - XNOR
  //   0x5
  //   - ADD
  //   0x6
  //   - SUB
  //   0x7
  //   Non-Native Unary Operations:
  //   operation
  //   - NEG
  //   0x7
  //   - NOT
  //   0x3
  //   - INC
  //   0x6
  //   - DEC
  //   0x7
  //   Non-Native Comparison Operations:
  //   operation
  //   - EQ
  //   0x7
  //   - NEQ
  //   0x7
  //   - LT
  //   0x7
  //   - LTE
  //   0x7
  //   Status:
  //   - overflow
  //   - carry
  //   - sign
  //   - zero
  //   16-Bit Extended ALU
  //   a
  //   b
  //   num
  //   0
  //   num
  //   0
  //   num
  //   1
  //   1
  //   num
  //   true if
  //   zero
  //   NOT zero
  //   sign
  //   sign OR zero
  //   0x1
  //   0x2
  //   0x4
  //   0x8
  //   output as
  //   result
  //   result
  //   result
  //   result
  //   only valid for operations on signed integers
  //   AND
  //   OR
  //   XOR
  //   ADD
  //   Chose basic ALU Operation
  //   result_invert
  //   b_negate
  //   <-
  //   AND
  //   NAND
  //   OR
  //   NOR
  //   XOR
  //   XNOR
  //   ADD
  //   SUB
  //   Chose extended ALU Operation
endmodule

module Shifter_16bit_by1 (
  input  shift_dir,
  input  [1:0] shift_in,
  input  [15:0] data_in,
  output [15:0] data_out
);

  wire multiplexer_1_out;
  wire [0:0] multiplexer_2_out;

  // Probe on data_in
  Multiplexer #(.enable("false")) multiplexer_1 (
    .in0(data_in[15]), .in1(data_in[0]), .out(multiplexer_1_out), .sel(shift_dir));
  Multiplexer #(.select(2), .enable("false")) multiplexer_2 (
    .in0(1'b0), .in1(1'b1), .in2(multiplexer_1_out), .in3(data_in[15]), .out(multiplexer_2_out[0]),
    .sel(shift_in));
  Multiplexer #(.width(16), .enable("false")) multiplexer_3 (
    .in0({data_in[14:0], multiplexer_2_out[0]}), .in1({multiplexer_2_out[0], data_in[15:1]}), .out(data_out),
    .sel(shift_dir));
  // Probe on shift_in
  // Probe on data_out

  // Notes on the sheet:
  //   0
  //   1
  //   shift_out
  //   msb
  //   shift_dir
  //   left
  //   right
  //   16-Bit Shifter (By 1 bit)
  //   shift_in
  //   0x0
  //   0x1
  //   0x2
  //   0x3
  //   0x0
  //   0x1
  //   Shift Left
  //   Shift Right
  //   shift_out_left
  //   shift_out_right
  //   shift_in
  //   msb
endmodule

module Shifter_16bit_by1_with_control (
  input  [2:0] operation,
  input  [15:0] data_in,
  output [15:0] data_out
);

  wire or_1_out, or_2_out, priority_encoder_1_p1, priority_encoder_1_p2, priority_encoder_1_p3,
       priority_encoder_1_p4, priority_encoder_1_p5, priority_encoder_1_p8, priority_encoder_1_p9;
  wire [1:0] priority_encoder_1_p6;

  or or_1 (or_1_out, priority_encoder_1_p5, priority_encoder_1_p3, priority_encoder_1_p2);
  // Probe on data_in
  nor nor_1 (or_1_out, priority_encoder_1_p4, priority_encoder_1_p1);
  Shifter_16bit_by1 shifter_16bit_by1_1 (
    .data_out(data_out), .data_in(data_in), .shift_in(priority_encoder_1_p6), .shift_dir(or_1_out));
  or or_2 (or_2_out, priority_encoder_1_p1, priority_encoder_1_p2);
  // Priority_Encoder #(.select(2)) priority_encoder_1: pin names not known; wires that end beside it: priority_encoder_1_p1, priority_encoder_1_p2, priority_encoder_1_p3, priority_encoder_1_p4, priority_encoder_1_p5, priority_encoder_1_p6, or_2_out, priority_encoder_1_p8, priority_encoder_1_p9, priority_encoder_1_p3, priority_encoder_1_p8
  or or_3 (priority_encoder_1_p9, priority_encoder_1_p4, priority_encoder_1_p5);
  // Probe on data_out
  Decoder #(.select(3), .enable("false")) decoder_1 (
    .out0(priority_encoder_1_p1), .out1(priority_encoder_1_p2), .out2(priority_encoder_1_p3),
    .out3(priority_encoder_1_p4), .out4(priority_encoder_1_p5), .sel(operation));  // open: out5, out6, out7
  // Probe on operation

  // Notes on the sheet:
  //   operation
  //   - SLL
  //   0x0
  //   - SRL
  //   0x1
  //   - SRA
  //   0x2
  //   - ROL
  //   0x3
  //   - ROR
  //   0x4
  //   Not Implemented
  //   0x5
  //   0x6
  //   0x7
  //   16-Bit Shifter (By 1 bit) with operation select
  //   shift_right
  //   shift_left
  //   shift_in_0
  //   shift_in_out
  //   shift_in_msb
  //   SLL
  //   SRL
  //   SRA
  //   ROL
  //   ROR
endmodule

module Shifter_16bit_byn (
  input  [2:0] operation,
  input  [15:0] data_in,
  input  [3:0] shamt,
  output [15:0] data_out
);

  wire [15:0] shifter_16bit_by1_with_control_1_data_out, shifter_16bit_by1_with_control_2_data_out,
       shifter_16bit_by1_with_control_3_data_out, shifter_16bit_by1_with_control_4_data_out,
       shifter_16bit_by1_with_control_5_data_out, shifter_16bit_by1_with_control_6_data_out,
       shifter_16bit_by1_with_control_7_data_out, shifter_16bit_by1_with_control_8_data_out,
       shifter_16bit_by1_with_control_9_data_out, shifter_16bit_by1_with_control_10_data_out,
       shifter_16bit_by1_with_control_11_data_out, shifter_16bit_by1_with_control_12_data_out,
       shifter_16bit_by1_with_control_13_data_out, shifter_16bit_by1_with_control_14_data_out,
       shifter_16bit_by1_with_control_15_data_out;

  // Probe on data_in
  Shifter_16bit_by1_with_control shifter_16bit_by1_with_control_1 (
    .data_out(shifter_16bit_by1_with_control_1_data_out), .data_in(data_in), .operation(operation));
  Multiplexer #(.select(4), .width(16), .enable("false")) multiplexer_1 (
    .in0(data_in), .in1(shifter_16bit_by1_with_control_1_data_out),
    .in2(shifter_16bit_by1_with_control_2_data_out), .in3(shifter_16bit_by1_with_control_3_data_out),
    .in4(shifter_16bit_by1_with_control_4_data_out), .in5(shifter_16bit_by1_with_control_5_data_out),
    .in6(shifter_16bit_by1_with_control_6_data_out), .in7(shifter_16bit_by1_with_control_7_data_out),
    .in8(shifter_16bit_by1_with_control_8_data_out), .in9(shifter_16bit_by1_with_control_9_data_out),
    .in10(shifter_16bit_by1_with_control_10_data_out), .in11(shifter_16bit_by1_with_control_11_data_out),
    .in12(shifter_16bit_by1_with_control_12_data_out), .in13(shifter_16bit_by1_with_control_13_data_out),
    .in14(shifter_16bit_by1_with_control_14_data_out), .in15(shifter_16bit_by1_with_control_15_data_out),
    .out(data_out), .sel(shamt));
  Shifter_16bit_by1_with_control shifter_16bit_by1_with_control_2 (
    .data_out(shifter_16bit_by1_with_control_2_data_out),
    .data_in(shifter_16bit_by1_with_control_1_data_out), .operation(operation));
  // Probe on data_out
  // Probe on shamt
  Shifter_16bit_by1_with_control shifter_16bit_by1_with_control_3 (
    .data_out(shifter_16bit_by1_with_control_3_data_out),
    .data_in(shifter_16bit_by1_with_control_2_data_out), .operation(operation));
  Shifter_16bit_by1_with_control shifter_16bit_by1_with_control_4 (
    .data_out(shifter_16bit_by1_with_control_4_data_out),
    .data_in(shifter_16bit_by1_with_control_3_data_out), .operation(operation));
  Shifter_16bit_by1_with_control shifter_16bit_by1_with_control_5 (
    .data_out(shifter_16bit_by1_with_control_5_data_out),
    .data_in(shifter_16bit_by1_with_control_4_data_out), .operation(operation));
  Shifter_16bit_by1_with_control shifter_16bit_by1_with_control_6 (
    .data_out(shifter_16bit_by1_with_control_6_data_out),
    .data_in(shifter_16bit_by1_with_control_5_data_out), .operation(operation));
  Shifter_16bit_by1_with_control shifter_16bit_by1_with_control_7 (
    .data_out(shifter_16bit_by1_with_control_7_data_out),
    .data_in(shifter_16bit_by1_with_control_6_data_out), .operation(operation));
  Shifter_16bit_by1_with_control shifter_16bit_by1_with_control_8 (
    .data_out(shifter_16bit_by1_with_control_8_data_out),
    .data_in(shifter_16bit_by1_with_control_7_data_out), .operation(operation));
  Shifter_16bit_by1_with_control shifter_16bit_by1_with_control_9 (
    .data_out(shifter_16bit_by1_with_control_9_data_out),
    .data_in(shifter_16bit_by1_with_control_8_data_out), .operation(operation));
  Shifter_16bit_by1_with_control shifter_16bit_by1_with_control_10 (
    .data_out(shifter_16bit_by1_with_control_10_data_out),
    .data_in(shifter_16bit_by1_with_control_9_data_out), .operation(operation));
  Shifter_16bit_by1_with_control shifter_16bit_by1_with_control_11 (
    .data_out(shifter_16bit_by1_with_control_11_data_out),
    .data_in(shifter_16bit_by1_with_control_10_data_out), .operation(operation));
  Shifter_16bit_by1_with_control shifter_16bit_by1_with_control_12 (
    .data_out(shifter_16bit_by1_with_control_12_data_out),
    .data_in(shifter_16bit_by1_with_control_11_data_out), .operation(operation));
  Shifter_16bit_by1_with_control shifter_16bit_by1_with_control_13 (
    .data_out(shifter_16bit_by1_with_control_13_data_out),
    .data_in(shifter_16bit_by1_with_control_12_data_out), .operation(operation));
  Shifter_16bit_by1_with_control shifter_16bit_by1_with_control_14 (
    .data_out(shifter_16bit_by1_with_control_14_data_out),
    .data_in(shifter_16bit_by1_with_control_13_data_out), .operation(operation));
  Shifter_16bit_by1_with_control shifter_16bit_by1_with_control_15 (
    .data_out(shifter_16bit_by1_with_control_15_data_out),
    .data_in(shifter_16bit_by1_with_control_14_data_out), .operation(operation));

  // Notes on the sheet:
  //   operation
  //   - SLL
  //   0x0
  //   0x1
  //   - SRL
  //   - SRA
  //   0x2
  //   - ROL
  //   0x3
  //   - ROR
  //   0x4
  //   Not Implemented
  //   0x5
  //   0x6
  //   0x7
  //   16-Bit Shifter
endmodule

module PLA_Example (
  input  A,
  input  B,
  input  C,
  output D
);

  wire and_1_out, and_2_out, and_3_out, not_1_out, not_2_out, not_3_out;

  not not_1 (not_1_out, A);
  not not_2 (not_2_out, B);
  not not_3 (not_3_out, C);
  and and_1 (and_1_out, A, not_2_out, not_3_out);
  and and_2 (and_2_out, not_1_out, B, not_3_out);
  and and_3 (and_3_out, not_1_out, not_2_out, C);
  or or_1 (D, and_3_out, and_2_out, and_1_out);

  // Notes on the sheet:
  //   PLA (Programmable Logic Array)
  //   Boolean Expression:
  //   AND ->
  //   i.e. minterms; product
  //   AB'C'
  //   AB'C' OR A'BC' OR A'B'C = XOR(A,B,C)
  //   (exactly one of three)
  //   A'BC'
  //   A'B'C
  //   OR ^
  //   i.e. maxterms; sum
  //   A
  //   NOT A
  //   B
  //   NOT B
  //   C
  //   NOT C
endmodule

module Overflow_Detect_16bit (
  input  [15:0] a,
  input  [15:0] b,
  input  [15:0] result,
  output overflow
);

  wire bitselector_1_out, bitselector_2_out, bitselector_3_out, xnor_1_out, xnor_2_out;

  // Probe on a
  // Probe on b
  // Probe on result
  BitSelector #(.width(16)) bitselector_1 (.in(a), .out(bitselector_1_out), .sel(4'b1111));
  BitSelector #(.width(16)) bitselector_2 (.in(b), .out(bitselector_2_out), .sel(4'b1111));
  BitSelector #(.width(16)) bitselector_3 (.in(result), .out(bitselector_3_out), .sel(4'b1111));
  xnor xnor_1 (xnor_1_out, bitselector_1_out, bitselector_2_out);
  xnor xnor_2 (xnor_2_out, bitselector_2_out, bitselector_3_out);
  and and_1 (overflow, xnor_1_out, ~xnor_2_out);  // AND_Gate

  // Notes on the sheet:
  //   16-Bit Signed Integer Overflow Detector
  //   a_sign
  //   b_sign
  //   result_sign
  //   ab_same_sign
  //   bresult_same_sign
endmodule

module Comparator_signed (
  input  [3:0] status,
  output lt,
  output eq,
  output gt
);

  xor xor_1 (lt, status[0], status[2]);
  nor nor_1 (gt, status[3], lt);

  assign eq = status[3];

  // Notes on the sheet:
  //   Assume status from ALU after A - B
  //   Status:
  //   - overflow
  //   - carry
  //   - sign
  //   - zero
  //   0x1
  //   0x2
  //   0x4
  //   0x8
  //   Two's Complement Signed Integer Comparator
  //   overflow
  //   carry
  //   sign
  //   zero
  //   Exactly One
  //   i.e. sign bit would be set if no overflow occured
endmodule

module Comparator_1bit_unsigned (
  input  A,
  input  B,
  output lt,
  output eq,
  output gt
);

  and and_1 (lt, ~A, B);  // AND_Gate
  xnor xnor_1 (eq, A, B);
  and and_2 (gt, A, ~B);  // AND_Gate

  // Notes on the sheet:
  //   1-bit Binary Comparator
  //   Exactly 1 of the comparator outputs will be true.
endmodule

module Comparator_4bit_unsigned (
  input  eq_in,
  input  gt_in,
  input  lt_in,
  input  [3:0] A,
  input  [3:0] B,
  output lt,
  output gt,
  output eq
);

  wire and_1_out, and_2_out, and_3_out, and_4_out, and_5_out, and_6_out, and_7_out,
       comparator_1bit_unsigned_1_eq, comparator_1bit_unsigned_1_gt, comparator_1bit_unsigned_2_eq,
       comparator_1bit_unsigned_2_gt, comparator_1bit_unsigned_3_eq, comparator_1bit_unsigned_3_gt,
       comparator_1bit_unsigned_4_eq, comparator_1bit_unsigned_4_gt;

  // Probe on A
  // Probe on B
  Comparator_1bit_unsigned comparator_1bit_unsigned_1 (
    .eq(comparator_1bit_unsigned_1_eq), .B(B[3]), .A(A[3]), .gt(comparator_1bit_unsigned_1_gt));  // open: lt
  Comparator_1bit_unsigned comparator_1bit_unsigned_2 (
    .eq(comparator_1bit_unsigned_2_eq), .B(B[2]), .A(A[2]), .gt(comparator_1bit_unsigned_2_gt));  // open: lt
  Comparator_1bit_unsigned comparator_1bit_unsigned_3 (
    .eq(comparator_1bit_unsigned_3_eq), .B(B[1]), .A(A[1]), .gt(comparator_1bit_unsigned_3_gt));  // open: lt
  Comparator_1bit_unsigned comparator_1bit_unsigned_4 (
    .eq(comparator_1bit_unsigned_4_eq), .B(B[0]), .A(A[0]), .gt(comparator_1bit_unsigned_4_gt));  // open: lt
  and and_1 (and_1_out, eq_in, comparator_1bit_unsigned_1_gt);
  and and_2 (and_2_out, eq_in, comparator_1bit_unsigned_1_eq);
  and and_3 (and_3_out, and_2_out, comparator_1bit_unsigned_2_gt);
  and and_4 (and_4_out, and_2_out, comparator_1bit_unsigned_2_eq);
  and and_5 (and_5_out, and_4_out, comparator_1bit_unsigned_3_gt);
  and and_6 (and_6_out, and_4_out, comparator_1bit_unsigned_3_eq);
  and and_7 (and_7_out, and_6_out, comparator_1bit_unsigned_4_gt);
  and and_8 (eq, and_6_out, comparator_1bit_unsigned_4_eq);
  or or_1 (gt, gt_in, and_1_out, and_3_out, and_5_out, and_7_out);
  nor nor_1 (lt, eq, gt);

  // Notes on the sheet:
  //   Unsigned Integer Comparator (4-bit)
  //   Exactly 1 of the comparator inputs must be true.
  //   Exactly 1 of the comparator outputs will be true.
  //   When used standalone or for most-significant-bits, set exactly eq_in to 1.
  //   A > B, if for some bit b, all higher bits are equal and b is greater.
  //   Bit 3
  //   Bit 2
  //   Bit 1
  //   Bit 0
  //   Needs further checking
  //   All Previous Equal
  //   All Previous Equal
  //   Implies greater-than
  //   All Previous Equal
  //   All Previous Equal
  //   Implies less-than
  //   All Previous Equal
endmodule

module Comparator_16bit_unsigned (
  input  [15:0] A,
  input  [15:0] B,
  output lt,
  output eq,
  output gt
);

  wire comparator_4bit_unsigned_1_eq, comparator_4bit_unsigned_1_gt, comparator_4bit_unsigned_1_lt,
       comparator_4bit_unsigned_2_eq, comparator_4bit_unsigned_2_gt, comparator_4bit_unsigned_2_lt,
       comparator_4bit_unsigned_3_eq, comparator_4bit_unsigned_3_gt, comparator_4bit_unsigned_3_lt;

  // Probe on A
  // Probe on B
  Comparator_4bit_unsigned comparator_4bit_unsigned_1 (
    .gt(comparator_4bit_unsigned_1_gt), .lt(comparator_4bit_unsigned_1_lt), .B(B[15:12]), .A(A[15:12]),
    .lt_in(1'b0), .gt_in(1'b0), .eq_in(1'b1), .eq(comparator_4bit_unsigned_1_eq));
  Comparator_4bit_unsigned comparator_4bit_unsigned_2 (
    .gt(comparator_4bit_unsigned_2_gt), .lt(comparator_4bit_unsigned_2_lt), .B(B[11:8]), .A(A[11:8]),
    .lt_in(comparator_4bit_unsigned_1_lt), .gt_in(comparator_4bit_unsigned_1_gt),
    .eq_in(comparator_4bit_unsigned_1_eq), .eq(comparator_4bit_unsigned_2_eq));
  Comparator_4bit_unsigned comparator_4bit_unsigned_3 (
    .gt(comparator_4bit_unsigned_3_gt), .lt(comparator_4bit_unsigned_3_lt), .B(B[7:4]), .A(A[7:4]),
    .lt_in(comparator_4bit_unsigned_2_lt), .gt_in(comparator_4bit_unsigned_2_gt),
    .eq_in(comparator_4bit_unsigned_2_eq), .eq(comparator_4bit_unsigned_3_eq));
  Comparator_4bit_unsigned comparator_4bit_unsigned_4 (
    .gt(gt), .lt(lt), .B(B[3:0]), .A(A[3:0]), .lt_in(comparator_4bit_unsigned_3_lt),
    .gt_in(comparator_4bit_unsigned_3_gt), .eq_in(comparator_4bit_unsigned_3_eq), .eq(eq));

  // Notes on the sheet:
  //   Unsigned Integer Comparator (16-bit)
  //   Exactly 1 of the comparator outputs will be true.
  //   Most-significant-nybble
  //   Least-significant-nybble
endmodule

module Comparator_16bit_premux (
  input  [3:0] status,
  input  [15:0] A,
  input  [15:0] B,
  output eq,
  output neq,
  output lt,
  output lte,
  output gt,
  output gte,
  output ltu,
  output lteu,
  output gtu,
  output gteu
);

  wire comparator_signed_1_eq;

  // Probe on A
  // Probe on A
  // Probe on B
  // Probe on B
  Comparator_signed comparator_signed_1 (.eq(comparator_signed_1_eq), .lt(lt), .status(status), .gt(gt));
  Comparator_16bit_unsigned comparator_16bit_unsigned_1 (.gt(gtu), .eq(eq), .lt(ltu), .B(B), .A(A));
  not not_1 (neq, eq);
  or or_1 (lte, comparator_signed_1_eq, lt);
  or or_2 (gte, gt, comparator_signed_1_eq);
  or or_3 (lteu, eq, ltu);
  or or_4 (gteu, gtu, eq);

  // Notes on the sheet:
  //   Assume status from ALU after A - B
  //   Status:
  //   - overflow
  //   - carry
  //   - sign
  //   - zero
  //   16-bit Integer Comparator (Pre-Mux)
  //   0x1
  //   0x2
  //   0x4
  //   0x8
  //   Signed
  //   Unsigned
  //   Signed
  //   Unsigned
  //   Signed Comparator
  //   Unsigned Comparator
  //   Equal
  //   Not Equal
  //   Sign-Independent
  //   Signed
  //   Unsigned
endmodule

module Comparator_16bit (
  input  [15:0] A,
  input  [2:0] operation,
  input  [15:0] B,
  input  [3:0] status,
  output compare
);

  wire comparator_16bit_premux_1_eq, comparator_16bit_premux_1_gt, comparator_16bit_premux_1_gtu,
       comparator_16bit_premux_1_lt, comparator_16bit_premux_1_lte, comparator_16bit_premux_1_lteu,
       comparator_16bit_premux_1_ltu, comparator_16bit_premux_1_neq;

  // Probe on A
  // Probe on A
  // Probe on B
  // Probe on B
  Comparator_16bit_premux comparator_16bit_premux_1 (
    .neq(comparator_16bit_premux_1_neq), .lt(comparator_16bit_premux_1_lt), .A(A),
    .lteu(comparator_16bit_premux_1_lteu), .B(B), .lte(comparator_16bit_premux_1_lte),
    .ltu(comparator_16bit_premux_1_ltu), .status(status), .gtu(comparator_16bit_premux_1_gtu),
    .eq(comparator_16bit_premux_1_eq), .gt(comparator_16bit_premux_1_gt));  // open: gteu, gte
  // Probe on operation
  Multiplexer #(.select(3), .enable("false")) multiplexer_1 (
    .in0(comparator_16bit_premux_1_eq), .in1(comparator_16bit_premux_1_neq),
    .in2(comparator_16bit_premux_1_lt), .in3(comparator_16bit_premux_1_lte),
    .in4(comparator_16bit_premux_1_ltu), .in5(comparator_16bit_premux_1_lteu),
    .in6(comparator_16bit_premux_1_gt), .in7(comparator_16bit_premux_1_gtu), .out(compare), .sel(operation));

  // Notes on the sheet:
  //   Assume status from ALU after A - B
  //   - overflow
  //   - carry
  //   - sign
  //   - zero
  //   operation:
  //   - EQ
  //   - NEQ
  //   - LT
  //   - LTE
  //   - LTU
  //   - LTEU
  //   - GT
  //   - GTU
  //   16-bit Integer Comparator
  //   status:
  //   0x1
  //   0x2
  //   0x4
  //   0x8
  //   0x0
  //   0x1
  //   0x2
  //   0x3
  //   0x4
  //   0x5
  //   0x6
  //   0x7
  //   Signed
  //   Unsigned
  //   Signed
  //   Unsigned
endmodule

module SR_Latch (
  input  set,
  input  reset,
  output value,
  output value_invert
);

  or or_1 (value, set, ~value_invert);  // OR_Gate
  or or_2 (value_invert, ~value, reset);  // OR_Gate

  // Notes on the sheet:
  //   SR Latch (Set-Reset)
  //   Unclocked; Stores 1 bit
endmodule

module D_Latch (
  input  clock,
  input  data_in,
  output data_out
);

  wire and_1_out, and_2_out;

  and and_1 (and_1_out, clock, data_in);
  and and_2 (and_2_out, clock, ~data_in);  // AND_Gate
  SR_Latch sr_latch_1 (.value(data_out), .reset(and_2_out), .set(and_1_out));  // open: value_invert

  // Notes on the sheet:
  //   D Latch (Data)
  //   Clocked; Stores 1 bit
  //   Store data bit when clock is high.
  //   New value available at output immediately.
endmodule

module D_Flip_Flop (
  input  clock,
  input  data_in,
  output data_out
);

  wire d_latch_1_data_out, not_1_out;

  D_Latch d_latch_1 (.data_out(d_latch_1_data_out), .data_in(data_in), .clock(clock));
  not not_1 (not_1_out, clock);
  D_Latch d_latch_2 (.data_out(data_out), .data_in(d_latch_1_data_out), .clock(not_1_out));
  // Probe on d_latch_1_data_out
  // Probe on data_out

  // Notes on the sheet:
  //   D Flip-Flop (Data/Delay)
  //   Clocked; Stores 1 bit
  //   Store data bit when clock is high.
  //   Old value available at output while clock remains high.
  //   New value available at output after clock low.
endmodule

module JK_Flip_Flop (
  input  J,
  input  clock,
  input  K,
  output value,
  output value_invert
);

  wire and_1_out, and_2_out;

  and and_1 (and_1_out, value_invert, J, clock);
  and and_2 (and_2_out, clock, K, value);
  nor nor_1 (value, and_1_out, value_invert);
  nor nor_2 (value_invert, value, and_2_out);

  // Notes on the sheet:
  //   JK Flip-Flop
endmodule

module JK_Flip_Flop_NAND (
  input  J,
  input  clock,
  input  K,
  output value,
  output value_invert
);

  wire nand_1_out, nand_2_out;

  nand nand_1 (nand_1_out, value_invert, clock);
  nand nand_2 (nand_2_out, clock, value);
  nand nand_3 (value, nand_1_out, value_invert);
  nand nand_4 (value_invert, value, nand_2_out);

  // Notes on the sheet:
  //   JK Flip-Flop
endmodule

module Memory_4bit (
  input  clock,
  input  [3:0] data_in,
  output [3:0] data_out
);

  D_Flip_Flop d_flip_flop_1 (.data_out(data_out[0]), .data_in(data_in[0]), .clock(clock));
  D_Flip_Flop d_flip_flop_2 (.data_out(data_out[1]), .data_in(data_in[1]), .clock(clock));
  D_Flip_Flop d_flip_flop_3 (.data_out(data_out[2]), .data_in(data_in[2]), .clock(clock));
  D_Flip_Flop d_flip_flop_4 (.data_out(data_out[3]), .data_in(data_in[3]), .clock(clock));

  // Notes on the sheet:
  //   4-Bit Memory Cell
  //   New value available on falling edge.
  //   Bit 0
  //   Bit 1
  //   Bit 2
  //   Bit 3
endmodule

module Memory_4bit_fast (
  input  [3:0] data_in,
  input  clock,
  output [3:0] data_out
);

  Register #(.width(4), .trigger("falling")) register_1 (.D(data_in), .clk(clock), .Q(data_out));  // open: en, clr

  // Notes on the sheet:
  //   4-Bit Memory Cell (Fast)
  //   New value available on falling edge.
  //   Reduces simulation load by using inbuilt circuits.
endmodule

module Memory_16bit (
  input  clock,
  input  [15:0] data_in,
  output [15:0] data_out
);

  // Probe on data_in
  Memory_4bit memory_4bit_1 (.data_out(data_out[3:0]), .data_in(data_in[3:0]), .clock(clock));
  Memory_4bit memory_4bit_2 (.data_out(data_out[7:4]), .data_in(data_in[7:4]), .clock(clock));
  Memory_4bit memory_4bit_3 (.data_out(data_out[11:8]), .data_in(data_in[11:8]), .clock(clock));
  Memory_4bit memory_4bit_4 (.data_out(data_out[15:12]), .data_in(data_in[15:12]), .clock(clock));
  // Probe on data_out

  // Notes on the sheet:
  //   16-Bit Memory Cell
  //   New value available on falling edge.
  //   Bits 0-3
  //   Bits 4-7
  //   Bits 8-11
  //   Bits 12-15
endmodule

module Memory_16bit_fast (
  input  [15:0] data_in,
  input  clock,
  output [15:0] data_out
);

  Register #(.width(16), .trigger("falling")) register_1 (.D(data_in), .clk(clock), .Q(data_out));  // open: en, clr

  // Notes on the sheet:
  //   16-Bit Memory Cell (Fast)
  //   New value available on falling edge.
  //   Reduces simulation load by using inbuilt circuits.
endmodule

module Register_File_16 (
  input  [3:0] B_index,
  input  [3:0] A_index,
  input  write_a,
  input  clock,
  input  [15:0] A_in,
  input  [15:0] PC_in,
  input  [15:0] Status_in,
  output [15:0] A_out,
  output [15:0] B_out,
  output [15:0] PC_out,
  output [15:0] Status_out
);

  wire and_1_out, demultiplexer_1_out0, demultiplexer_1_out1, demultiplexer_1_out2, demultiplexer_1_out3,
       demultiplexer_1_out4, demultiplexer_1_out5, demultiplexer_1_out6, demultiplexer_1_out7,
       demultiplexer_1_out8, demultiplexer_1_out9, demultiplexer_1_out10, demultiplexer_1_out11,
       demultiplexer_1_out12, demultiplexer_1_out13, demultiplexer_1_out14, demultiplexer_1_out15;
  wire [15:0] memory_16bit_fast_1_data_out, memory_16bit_fast_2_data_out, memory_16bit_fast_3_data_out,
       memory_16bit_fast_4_data_out, memory_16bit_fast_5_data_out, memory_16bit_fast_6_data_out,
       memory_16bit_fast_7_data_out, memory_16bit_fast_8_data_out, memory_16bit_fast_9_data_out,
       memory_16bit_fast_10_data_out, memory_16bit_fast_11_data_out, memory_16bit_fast_12_data_out,
       memory_16bit_fast_13_data_out, memory_16bit_fast_14_data_out, multiplexer_1_out;

  // Probe on B_index
  // Probe on A_index
  // Probe on A_in
  // Probe on PC_in
  and and_1 (and_1_out, clock, write_a);
  Demultiplexer #(.select(4), .enable("false")) demultiplexer_1 (
    .out0(demultiplexer_1_out0), .out1(demultiplexer_1_out1), .out2(demultiplexer_1_out2),
    .out3(demultiplexer_1_out3), .out4(demultiplexer_1_out4), .out5(demultiplexer_1_out5),
    .out6(demultiplexer_1_out6), .out7(demultiplexer_1_out7), .out8(demultiplexer_1_out8),
    .out9(demultiplexer_1_out9), .out10(demultiplexer_1_out10), .out11(demultiplexer_1_out11),
    .out12(demultiplexer_1_out12), .out13(demultiplexer_1_out13), .out14(demultiplexer_1_out14),
    .out15(demultiplexer_1_out15), .in(and_1_out), .sel(A_index));
  Multiplexer #(.width(16), .enable("false")) multiplexer_1 (
    .in0(PC_in), .in1(A_in), .out(multiplexer_1_out), .sel(demultiplexer_1_out14));
  Memory_16bit_fast memory_16bit_fast_1 (.data_out(memory_16bit_fast_1_data_out), .clock(clock), .data_in({16{1'b0}}));
  Memory_16bit_fast memory_16bit_fast_2 (
    .data_out(memory_16bit_fast_2_data_out), .clock(demultiplexer_1_out1), .data_in(A_in));
  Memory_16bit_fast memory_16bit_fast_3 (
    .data_out(memory_16bit_fast_3_data_out), .clock(demultiplexer_1_out2), .data_in(A_in));
  Memory_16bit_fast memory_16bit_fast_4 (
    .data_out(memory_16bit_fast_4_data_out), .clock(demultiplexer_1_out3), .data_in(A_in));
  Memory_16bit_fast memory_16bit_fast_5 (
    .data_out(memory_16bit_fast_5_data_out), .clock(demultiplexer_1_out4), .data_in(A_in));
  Memory_16bit_fast memory_16bit_fast_6 (
    .data_out(memory_16bit_fast_6_data_out), .clock(demultiplexer_1_out5), .data_in(A_in));
  Memory_16bit_fast memory_16bit_fast_7 (
    .data_out(memory_16bit_fast_7_data_out), .clock(demultiplexer_1_out6), .data_in(A_in));
  Memory_16bit_fast memory_16bit_fast_8 (
    .data_out(memory_16bit_fast_8_data_out), .clock(demultiplexer_1_out7), .data_in(A_in));
  Memory_16bit_fast memory_16bit_fast_9 (
    .data_out(memory_16bit_fast_9_data_out), .clock(demultiplexer_1_out8), .data_in(A_in));
  Memory_16bit_fast memory_16bit_fast_10 (
    .data_out(memory_16bit_fast_10_data_out), .clock(demultiplexer_1_out9), .data_in(A_in));
  Memory_16bit_fast memory_16bit_fast_11 (
    .data_out(memory_16bit_fast_11_data_out), .clock(demultiplexer_1_out10), .data_in(A_in));
  Memory_16bit_fast memory_16bit_fast_12 (
    .data_out(memory_16bit_fast_12_data_out), .clock(demultiplexer_1_out11), .data_in(A_in));
  Memory_16bit_fast memory_16bit_fast_13 (
    .data_out(memory_16bit_fast_13_data_out), .clock(demultiplexer_1_out12), .data_in(A_in));
  Memory_16bit_fast memory_16bit_fast_14 (
    .data_out(memory_16bit_fast_14_data_out), .clock(demultiplexer_1_out13), .data_in(A_in));
  Memory_16bit_fast memory_16bit_fast_15 (.data_out(PC_out), .clock(clock), .data_in(multiplexer_1_out));
  Memory_16bit_fast memory_16bit_fast_16 (.data_out(Status_out), .clock(clock), .data_in(Status_in));
  Multiplexer #(.select(4), .width(16), .enable("false")) multiplexer_2 (
    .in0(memory_16bit_fast_1_data_out), .in1(memory_16bit_fast_2_data_out),
    .in2(memory_16bit_fast_3_data_out), .in3(memory_16bit_fast_4_data_out),
    .in4(memory_16bit_fast_5_data_out), .in5(memory_16bit_fast_6_data_out),
    .in6(memory_16bit_fast_7_data_out), .in7(memory_16bit_fast_8_data_out),
    .in8(memory_16bit_fast_9_data_out), .in9(memory_16bit_fast_10_data_out),
    .in10(memory_16bit_fast_11_data_out), .in11(memory_16bit_fast_12_data_out),
    .in12(memory_16bit_fast_13_data_out), .in13(memory_16bit_fast_14_data_out), .in14(PC_out),
    .in15(Status_out), .out(A_out), .sel(A_index));
  Multiplexer #(.select(4), .width(16), .enable("false")) multiplexer_3 (
    .in0(memory_16bit_fast_1_data_out), .in1(memory_16bit_fast_2_data_out),
    .in2(memory_16bit_fast_3_data_out), .in3(memory_16bit_fast_4_data_out),
    .in4(memory_16bit_fast_5_data_out), .in5(memory_16bit_fast_6_data_out),
    .in6(memory_16bit_fast_7_data_out), .in7(memory_16bit_fast_8_data_out),
    .in8(memory_16bit_fast_9_data_out), .in9(memory_16bit_fast_10_data_out),
    .in10(memory_16bit_fast_11_data_out), .in11(memory_16bit_fast_12_data_out),
    .in12(memory_16bit_fast_13_data_out), .in13(memory_16bit_fast_14_data_out), .in14(PC_out),
    .in15(Status_out), .out(B_out), .sel(B_index));
  // Probe on A_out
  // Probe on B_out
  // Probe on PC_out

  // Notes on the sheet:
  //   16-Bit Register File
  //   Two registers can be read in a single clock.
  //   PC and Status register values are always available
  //   Two special-purpose registers are written each clock.
  //   One general-purpose register can be written each clock.
  //   General-purpose writes to register 0 or 15 are ignored.
  //   Choose Registers
  //   Control Signals
  //   Data In
  //   clock
  //   Register writes only occur on high clock.
  //   Updated register values only visible after next low clock.
  //   Choose
  //   Write Register
  //   Choose PC Source
  //   PC register input is either PC_in or A_in (if writing there)
  //   $0 - Zero
  //   $1
  //   $2
  //   $3
  //   $4
  //   $5
  //   $6
  //   $7
  //   $8
  //   $9
  //   $10
  //   $11
  //   $12
  //   $13
  //   $14 - PC
  //   $15 - Status
  //   Choose
  //   Read Register A
  //   Choose
  //   Read Register B
  //   B_index
  //   A_index
  //   Data Out
endmodule

module RAM_32bit_2bitaddress (
  input  [1:0] address,
  input  clock,
  input  [31:0] data_in,
  output [31:0] data_out
);

  wire demultiplexer_1_out0, demultiplexer_1_out1, demultiplexer_1_out2, demultiplexer_1_out3;
  wire [31:0] register_1_q, register_2_q, register_3_q, register_4_q;

  Demultiplexer #(.select(2), .enable("false")) demultiplexer_1 (
    .out0(demultiplexer_1_out0), .out1(demultiplexer_1_out1), .out2(demultiplexer_1_out2),
    .out3(demultiplexer_1_out3), .in(clock), .sel(address));
  Register #(.width(32), .trigger("falling")) register_1 (
    .D(data_in), .clk(demultiplexer_1_out0), .Q(register_1_q));  // open: en, clr
  Register #(.width(32), .trigger("falling")) register_2 (
    .D(data_in), .clk(demultiplexer_1_out1), .Q(register_2_q));  // open: en, clr
  Register #(.width(32), .trigger("falling")) register_3 (
    .D(data_in), .clk(demultiplexer_1_out2), .Q(register_3_q));  // open: en, clr
  Register #(.width(32), .trigger("falling")) register_4 (
    .D(data_in), .clk(demultiplexer_1_out3), .Q(register_4_q));  // open: en, clr
  Multiplexer #(.select(2), .width(32), .enable("false")) multiplexer_1 (
    .in0(register_1_q), .in1(register_2_q), .in2(register_3_q), .in3(register_4_q), .out(data_out),
    .sel(address));

  // Notes on the sheet:
  //   4x 32-bit SRAM with 2-bit address
endmodule

module RAM_32bit_4bitaddress (
  input  [3:0] address,
  input  clock,
  input  [31:0] data_in,
  output [31:0] data_out
);

  wire demultiplexer_1_out0, demultiplexer_1_out1, demultiplexer_1_out2, demultiplexer_1_out3;
  wire [31:0] ram_32bit_2bitaddress_1_data_out, ram_32bit_2bitaddress_2_data_out,
       ram_32bit_2bitaddress_3_data_out, ram_32bit_2bitaddress_4_data_out;

  Demultiplexer #(.select(2), .enable("false")) demultiplexer_1 (
    .out0(demultiplexer_1_out0), .out1(demultiplexer_1_out1), .out2(demultiplexer_1_out2),
    .out3(demultiplexer_1_out3), .in(clock), .sel(address[3:2]));
  RAM_32bit_2bitaddress ram_32bit_2bitaddress_1 (
    .data_in(data_in), .data_out(ram_32bit_2bitaddress_1_data_out), .clock(demultiplexer_1_out0),
    .address(address[1:0]));
  RAM_32bit_2bitaddress ram_32bit_2bitaddress_2 (
    .data_in(data_in), .data_out(ram_32bit_2bitaddress_2_data_out), .clock(demultiplexer_1_out1),
    .address(address[1:0]));
  RAM_32bit_2bitaddress ram_32bit_2bitaddress_3 (
    .data_in(data_in), .data_out(ram_32bit_2bitaddress_3_data_out), .clock(demultiplexer_1_out2),
    .address(address[1:0]));
  RAM_32bit_2bitaddress ram_32bit_2bitaddress_4 (
    .data_in(data_in), .data_out(ram_32bit_2bitaddress_4_data_out), .clock(demultiplexer_1_out3),
    .address(address[1:0]));
  Multiplexer #(.select(2), .width(32), .enable("false")) multiplexer_1 (
    .in0(ram_32bit_2bitaddress_1_data_out), .in1(ram_32bit_2bitaddress_2_data_out),
    .in2(ram_32bit_2bitaddress_3_data_out), .in3(ram_32bit_2bitaddress_4_data_out), .out(data_out),
    .sel(address[3:2]));

  // Notes on the sheet:
  //   16x 32-bit SRAM with 4-bit address
endmodule

module RAM_32bit_6bitaddress (
  input  [5:0] address,
  input  clock,
  input  [31:0] data_in,
  output [31:0] data_out
);

  wire demultiplexer_1_out0, demultiplexer_1_out1, demultiplexer_1_out2, demultiplexer_1_out3;
  wire [31:0] ram_32bit_4bitaddress_1_data_out, ram_32bit_4bitaddress_2_data_out,
       ram_32bit_4bitaddress_3_data_out, ram_32bit_4bitaddress_4_data_out;

  Demultiplexer #(.select(2), .enable("false")) demultiplexer_1 (
    .out0(demultiplexer_1_out0), .out1(demultiplexer_1_out1), .out2(demultiplexer_1_out2),
    .out3(demultiplexer_1_out3), .in(clock), .sel(address[5:4]));
  RAM_32bit_4bitaddress ram_32bit_4bitaddress_1 (
    .data_in(data_in), .data_out(ram_32bit_4bitaddress_1_data_out), .address(address[3:0]),
    .clock(demultiplexer_1_out0));
  RAM_32bit_4bitaddress ram_32bit_4bitaddress_2 (
    .data_in(data_in), .data_out(ram_32bit_4bitaddress_2_data_out), .address(address[3:0]),
    .clock(demultiplexer_1_out1));
  RAM_32bit_4bitaddress ram_32bit_4bitaddress_3 (
    .data_in(data_in), .data_out(ram_32bit_4bitaddress_3_data_out), .address(address[3:0]),
    .clock(demultiplexer_1_out2));
  RAM_32bit_4bitaddress ram_32bit_4bitaddress_4 (
    .data_in(data_in), .data_out(ram_32bit_4bitaddress_4_data_out), .address(address[3:0]),
    .clock(demultiplexer_1_out3));
  Multiplexer #(.select(2), .width(32), .enable("false")) multiplexer_1 (
    .in0(ram_32bit_4bitaddress_1_data_out), .in1(ram_32bit_4bitaddress_2_data_out),
    .in2(ram_32bit_4bitaddress_3_data_out), .in3(ram_32bit_4bitaddress_4_data_out), .out(data_out),
    .sel(address[5:4]));

  // Notes on the sheet:
  //   64x 32-bit SRAM with 6-bit address
endmodule

module RAM_32bit_8bitaddress (
  input  [7:0] address,
  input  clock,
  input  [31:0] data_in,
  output [31:0] data_out
);

  wire demultiplexer_1_out0, demultiplexer_1_out1, demultiplexer_1_out2, demultiplexer_1_out3;
  wire [31:0] ram_32bit_6bitaddress_1_data_out, ram_32bit_6bitaddress_2_data_out,
       ram_32bit_6bitaddress_3_data_out, ram_32bit_6bitaddress_4_data_out;

  Demultiplexer #(.select(2), .enable("false")) demultiplexer_1 (
    .out0(demultiplexer_1_out0), .out1(demultiplexer_1_out1), .out2(demultiplexer_1_out2),
    .out3(demultiplexer_1_out3), .in(clock), .sel(address[7:6]));
  RAM_32bit_6bitaddress ram_32bit_6bitaddress_1 (
    .data_in(data_in), .clock(demultiplexer_1_out0), .address(address[5:0]),
    .data_out(ram_32bit_6bitaddress_1_data_out));
  RAM_32bit_6bitaddress ram_32bit_6bitaddress_2 (
    .data_in(data_in), .clock(demultiplexer_1_out1), .address(address[5:0]),
    .data_out(ram_32bit_6bitaddress_2_data_out));
  RAM_32bit_6bitaddress ram_32bit_6bitaddress_3 (
    .data_in(data_in), .clock(demultiplexer_1_out2), .address(address[5:0]),
    .data_out(ram_32bit_6bitaddress_3_data_out));
  RAM_32bit_6bitaddress ram_32bit_6bitaddress_4 (
    .data_in(data_in), .clock(demultiplexer_1_out3), .address(address[5:0]),
    .data_out(ram_32bit_6bitaddress_4_data_out));
  Multiplexer #(.select(2), .width(32), .enable("false")) multiplexer_1 (
    .in0(ram_32bit_6bitaddress_1_data_out), .in1(ram_32bit_6bitaddress_2_data_out),
    .in2(ram_32bit_6bitaddress_3_data_out), .in3(ram_32bit_6bitaddress_4_data_out), .out(data_out),
    .sel(address[7:6]));

  // Notes on the sheet:
  //   256x 32-bit SRAM with 8-bit address
endmodule

module ZeroExtend_8bit_to_32bit (
  input  [7:0] in8,
  output [31:0] out32
);

  // Probe on in8
  // Probe on {{24{1'b0}}, in8}

  assign out32 = {{24{1'b0}}, in8};

  // Notes on the sheet:
  //   8-bit to 32-bit Zero Extender
endmodule

module SignExtend_8bit_to_32bit (
  input  [7:0] in8,
  output [31:0] out32
);

  // Probe on in8
  // Probe on {{25{in8[7]}}, in8[6:0]}

  assign out32 = {{25{in8[7]}}, in8[6:0]};

  // Notes on the sheet:
  //   8-bit to 32-bit Sign Extender
endmodule

module ZeroExtend_16bit_to_32bit (
  input  [15:0] in16,
  output [31:0] out32
);

  // Probe on in16
  // Probe on {{16{1'b0}}, in16}

  assign out32 = {{16{1'b0}}, in16};

  // Notes on the sheet:
  //   16-bit to 32-bit Zero Extender
endmodule

module SignExtend_16bit_to_32bit (
  input  [15:0] in16,
  output [31:0] out32
);

  // Probe on in16
  // Probe on {{17{in16[15]}}, in16[14:0]}

  assign out32 = {{17{in16[15]}}, in16[14:0]};

  // Notes on the sheet:
  //   16-bit to 32-bit Sign Extender
endmodule

module Extract_from_32bit (
  input  [1:0] offset,
  input  [2:0] operation,
  input  [31:0] in32,
  output [31:0] out32
);

  wire [7:0] multiplexer_2_out;
  wire [15:0] multiplexer_1_out;
  wire [31:0] signextend_8bit_to_32bit_1_out32, signextend_16bit_to_32bit_1_out32,
       zeroextend_8bit_to_32bit_1_out32, zeroextend_16bit_to_32bit_1_out32;

  Multiplexer #(.width(16), .enable("false")) multiplexer_1 (
    .in0(in32[15:0]), .in1(in32[31:16]), .out(multiplexer_1_out), .sel(offset[0]));
  Multiplexer #(.select(2), .width(8), .enable("false")) multiplexer_2 (
    .in0(in32[7:0]), .in1(in32[15:8]), .in2(in32[23:16]), .in3(in32[31:24]), .out(multiplexer_2_out),
    .sel(offset));
  SignExtend_16bit_to_32bit signextend_16bit_to_32bit_1 (
    .out32(signextend_16bit_to_32bit_1_out32), .in16(multiplexer_1_out));
  ZeroExtend_16bit_to_32bit zeroextend_16bit_to_32bit_1 (
    .out32(zeroextend_16bit_to_32bit_1_out32), .in16(multiplexer_1_out));
  SignExtend_8bit_to_32bit signextend_8bit_to_32bit_1 (
    .in8(multiplexer_2_out), .out32(signextend_8bit_to_32bit_1_out32));
  ZeroExtend_8bit_to_32bit zeroextend_8bit_to_32bit_1 (
    .in8(multiplexer_2_out), .out32(zeroextend_8bit_to_32bit_1_out32));
  Multiplexer #(.select(3), .width(32), .enable("false")) multiplexer_3 (
    .in0(in32), .in1(signextend_16bit_to_32bit_1_out32), .in2(zeroextend_16bit_to_32bit_1_out32),
    .in3(signextend_8bit_to_32bit_1_out32), .in4(zeroextend_8bit_to_32bit_1_out32), .in5({32{1'b1}}),
    .in6({32{1'b1}}), .in7({32{1'b1}}), .out(out32), .sel(operation));

  // Notes on the sheet:
  //   Extract 8/16/32 bit field from 32-bit value
  //   - read32
  //   - read16
  //   - read16u
  //   - read8
  //   - read8u
  //   operation:
  //   0x0
  //   0x1
  //   0x2
  //   0x3
  //   0x4
  //   0xFFFFFFFF Otherwise
  //   (Sign-extended)
  //   (Zero-extended)
  //   (Sign-extended)
  //   (Zero-extended)
  //   Low 1 bit
  //   Low 2 bits
  //   <- Choose Half-Word
  //   <- Choose Byte
  //   Error
  //   Unknown Operation
endmodule

module Replace_in_32bit (
  input  [1:0] offset,
  input  [1:0] operation,
  input  [31:0] in_replace,
  input  [31:0] in_original,
  output [31:0] out_result
);

  wire [31:0] multiplexer_1_out, multiplexer_2_out;

  Multiplexer #(.width(32), .enable("false")) multiplexer_1 (
    .in0({in_original[31:16], in_replace[15:0]}), .in1({in_replace[15:0], in_original[15:0]}),
    .out(multiplexer_1_out), .sel(offset[0]));
  Multiplexer #(.select(2), .width(32), .enable("false")) multiplexer_2 (
    .in0({in_original[31:8], in_replace[7:0]}),
    .in1({in_original[31:16], in_replace[7:0], in_original[7:0]}),
    .in2({in_original[31:24], in_replace[7:0], in_original[15:0]}),
    .in3({in_replace[7:0], in_original[23:0]}), .out(multiplexer_2_out), .sel(offset));
  Multiplexer #(.select(2), .width(32), .enable("false")) multiplexer_3 (
    .in0(in_replace), .in1(multiplexer_1_out), .in2(multiplexer_2_out), .in3({32{1'b1}}), .out(out_result),
    .sel(operation));

  // Notes on the sheet:
  //   Replace 8/16/32 bit field in 32-bit value
  //   Replace field at offset (into in_original) with value in_replace.
  //   operation:
  //   - write32
  //   - write16
  //   - write8
  //   0x0
  //   0x1
  //   0x2
  //   0xFFFFFFFF Otherwise
  //   Lower 32 bits from in_replace
  //   Lower 16 bits from in_replace
  //   Lower 8 bits from in_replace
  //   Replace Lower Half-Word
  //   Replace Upper Half-Word
  //   Replace Byte 0
  //   Replace Byte 1
  //   Replace Byte 2
  //   Replace Byte 3
  //   Extract lower 8/16 bits
  //   Low 1 bit
  //   Low 2 bits
  //   Replace 32 bits
  //   Replace 16 bits
  //   Replace 8 bits
  //   Error
  //   Unknown Operation
endmodule

module AlignmentChecker (
  input  [31:0] address,
  output align_8bit,
  output align_16bit,
  output align_32bit
);

  not not_1 (align_16bit, address[0]);
  nor nor_1 (align_32bit, address[0], address[1]);

  assign align_8bit = 1'b1;

  // Notes on the sheet:
  //   Alignment Checker
  //   Checks the alignment of a 32-bit byte address.
endmodule

module AddressChecker (
  input  [4:0] address_bits,
  input  [31:0] address,
  input  [1:0] access_size,
  output in_range,
  output aligned
);

  wire alignmentchecker_1_align_16bit, alignmentchecker_1_align_32bit, and_1_out, and_2_out, decoder_1_out0,
       decoder_1_out1, decoder_1_out2;
  wire [31:0] shifter_1_out;

  // Probe on address_bits
  AlignmentChecker alignmentchecker_1 (
    .align_32bit(alignmentchecker_1_align_32bit), .align_16bit(alignmentchecker_1_align_16bit),
    .address(address));  // open: align_8bit
  Decoder #(.select(2)) decoder_1 (
    .out0(decoder_1_out0), .out1(decoder_1_out1), .out2(decoder_1_out2), .sel(access_size));  // open: out3, en
  Shifter #(.width(32)) shifter_1 (.in(32'h1), .\dist (address_bits), .out(shifter_1_out));
  Comparator #(.width(32), .mode("unsigned")) comparator_1 (
    .a(shifter_1_out), .b(address), .gt(in_range));  // open: eq, lt
  and and_1 (and_1_out, alignmentchecker_1_align_32bit, decoder_1_out0);
  and and_2 (and_2_out, alignmentchecker_1_align_16bit, decoder_1_out1);
  or or_1 (aligned, and_2_out, decoder_1_out2, and_1_out);

  // Notes on the sheet:
  //   Address Checker
  //   Validates a memory access at a given 32-bit address
  //   address_bits is number of addressable bits
  //   - 32-bit
  //   - 16-bit
  //   - 8-bit
  //   access_size:
  //   0x0
  //   0x1
  //   0x2
  //   Range
  //   Alignment
  //   32-bit
  //   16-bit
  //   8-bit
endmodule

module RAM_Controller_32bit (
  input  [31:0] address_in,
  input  [31:0] data_in,
  input  [31:0] ram_data_in,
  input  clock,
  input  [2:0] operation,
  input  [4:0] ram_size,
  output [31:0] ram_address,
  output [31:0] ram_data_out,
  output [31:0] data_out,
  output ram_clock,
  output [1:0] error
);

  wire addresschecker_1_aligned, addresschecker_1_in_range, decoder_1_out0, decoder_1_out1, decoder_1_out2,
       decoder_1_out3, decoder_1_out4, decoder_1_out5, decoder_1_out6, decoder_1_out7, or_4_out,
       priority_encoder_1_p2, priority_encoder_1_p3, priority_encoder_1_p4;
  wire [1:0] priority_encoder_1_p1, priority_encoder_3_out;
  wire [2:0] priority_encoder_2_out;

  AddressChecker addresschecker_1 (
    .in_range(addresschecker_1_in_range), .address(address_in), .access_size(priority_encoder_1_p1),
    .aligned(addresschecker_1_aligned), .address_bits(ram_size));
  Decoder #(.select(3)) decoder_1 (
    .out0(decoder_1_out0), .out1(decoder_1_out1), .out2(decoder_1_out2), .out3(decoder_1_out3),
    .out4(decoder_1_out4), .out5(decoder_1_out5), .out6(decoder_1_out6), .out7(decoder_1_out7),
    .sel(operation));  // open: en
  // Priority_Encoder #(.select(2)) priority_encoder_1: pin names not known; wires that end beside it: priority_encoder_1_p1, priority_encoder_1_p2, priority_encoder_1_p3, priority_encoder_1_p4
  Extract_from_32bit extract_from_32bit_1 (
    .out32(data_out), .in32(ram_data_in), .operation(priority_encoder_2_out), .offset(address_in[1:0]));
  not not_1 (error[0], addresschecker_1_in_range);
  not not_2 (error[1], addresschecker_1_aligned);
  Priority_Encoder priority_encoder_2 (
    .in0(decoder_1_out0), .in1(decoder_1_out1), .in2(decoder_1_out2), .in3(decoder_1_out3),
    .in4(decoder_1_out4), .out(priority_encoder_2_out));  // open: in5, in6, in7, en_in
  LED OUT_OF_RANGE (.in(error[0]));
  LED UNALIGNED_ADDRESS (.in(error[1]));
  Replace_in_32bit replace_in_32bit_1 (
    .in_original(ram_data_in), .operation(priority_encoder_3_out), .in_replace(data_in),
    .out_result(ram_data_out), .offset(address_in[1:0]));
  or or_1 (priority_encoder_1_p2, decoder_1_out0, decoder_1_out5);
  or or_2 (priority_encoder_1_p3, decoder_1_out6, decoder_1_out2, decoder_1_out1);
  Priority_Encoder #(.select(2)) priority_encoder_3 (
    .in0(decoder_1_out5), .in1(decoder_1_out6), .in2(decoder_1_out7), .out(priority_encoder_3_out));  // open: in3
  or or_3 (priority_encoder_1_p4, decoder_1_out3, decoder_1_out4, decoder_1_out7);
  and and_1 (ram_clock, clock, or_4_out);
  or or_4 (or_4_out, decoder_1_out5, decoder_1_out6, decoder_1_out7);

  assign ram_address = {2'b00, address_in[31:2]};

  // Notes on the sheet:
  //   32-bit RAM Controller
  //   Controls read/write operations on a 32-bit memory cell with up to 32 address bits (30 bits addressable).
  //   ram_size is 2^n addressable 32-bit words (n between 0-32 inclusive)
  //   address_in is Bytes (8-bit), ram_address is Words (32-bit)
  //   - read32
  //   - read16
  //   - read16u
  //   - read8
  //   - read8u
  //   - write32
  //   - write16
  //   - write8
  //   - OutOfRange
  //   - Unaligned
  //   operation:
  //   0x0
  //   0x1
  //   0x2
  //   0x3
  //   0x4
  //   0x5
  //   0x6
  //   0x7
  //   error:
  //   0x1
  //   0x2
  //   Controller Interface
  //   32-bit Access
  //   16-bit Access
  //   8-bit Access
  //   Lower two address bits
  //   Error Checking
  //   Byte Address -> Word Address
  //   (address >> 2)
  //   read32
  //   read16
  //   read16u
  //   read8
  //   read8u
  //   write32
  //   write16
  //   write8
  //   RAM Chip Interface
endmodule

module RAM_1KB_A (
  input  [7:0] address,
  input  [31:0] data_in,
  input  clock,
  output [31:0] data_out
);

  wire and_1_out, s_r_ff_1_q;
  wire [31:0] register_1_q;

  Register #(.width(32), .trigger("high")) register_1 (
    .D(data_in), .en(1'b1), .clk(clock), .Q(register_1_q));  // open: clr
  S_R_Flip_Flop #(.trigger("high")) s_r_ff_1 (
    .Q(s_r_ff_1_q), .reset(and_1_out), .preset(clock));  // open: S, R, clk, Qn
  RAM #(.dataWidth(32), .trigger("high"), .databus("bibus")) ram_1 (
    .addr(address), .we(and_1_out), .oe(1'b1), .din(register_1_q), .dout(data_out));
  and and_1 (and_1_out, ~clock, s_r_ff_1_q);  // AND_Gate

  // Notes on the sheet:
  //   1KB RAM Module (Instance A)
  //   Data is read on address change.
  //   Data is written on falling clock edge.
  //   Simulator bug causes address 0x0 to be set to 0xFFFFFFFF when restarting simulation.
  //   Buffer new value
  //   Write on falling edge
  //   Only write if clock pending
endmodule

module RAM_1KB_B (
  input  [7:0] address,
  input  [31:0] data_in,
  input  clock,
  output [31:0] data_out
);

  wire and_1_out, s_r_ff_1_q;
  wire [31:0] register_1_q;

  Register #(.width(32), .trigger("high")) register_1 (
    .D(data_in), .en(1'b1), .clk(clock), .Q(register_1_q));  // open: clr
  S_R_Flip_Flop #(.trigger("high")) s_r_ff_1 (
    .Q(s_r_ff_1_q), .reset(and_1_out), .preset(clock));  // open: S, R, clk, Qn
  RAM #(.dataWidth(32), .trigger("high"), .databus("bibus")) ram_1 (
    .addr(address), .we(and_1_out), .oe(1'b1), .din(register_1_q), .dout(data_out));
  and and_1 (and_1_out, ~clock, s_r_ff_1_q);  // AND_Gate

  // Notes on the sheet:
  //   1KB RAM Module (Instance B)
  //   Data is read on address change.
  //   Data is written on falling clock edge.
  //   Simulator bug causes address 0x0 to be set to 0xFFFFFFFF when restarting simulation.
  //   Buffer new value
  //   Write on falling edge
  //   Only write if clock pending
endmodule

module RAM_1KB_with_controller_A (
  input  [31:0] address,
  input  [31:0] data_in,
  input  clock,
  input  [2:0] operation,
  output [1:0] error,
  output [31:0] data_out
);

  wire ram_controller_32bit_1_ram_clock;
  wire [7:0] bitselector_1_out;
  wire [31:0] ram_1kb_a_1_data_out, ram_controller_32bit_1_ram_address, ram_controller_32bit_1_ram_data_out;

  RAM_Controller_32bit ram_controller_32bit_1 (
    .operation(operation), .ram_clock(ram_controller_32bit_1_ram_clock), .data_in(data_in),
    .data_out(data_out), .clock(clock), .address_in(address), .ram_data_in(ram_1kb_a_1_data_out),
    .ram_size(5'b01010), .ram_address(ram_controller_32bit_1_ram_address),
    .ram_data_out(ram_controller_32bit_1_ram_data_out), .error(error));
  BitSelector #(.width(32), .group(8)) bitselector_1 (
    .in(ram_controller_32bit_1_ram_address), .out(bitselector_1_out), .sel(2'b00));
  RAM_1KB_A ram_1kb_a_1 (
    .data_out(ram_1kb_a_1_data_out), .data_in(ram_controller_32bit_1_ram_data_out),
    .clock(ram_controller_32bit_1_ram_clock), .address(bitselector_1_out));

  // Notes on the sheet:
  //   1KB RAM Module With Controller (Instance A)
  //   Data is read on address change.
  //   Data is written on falling clock edge.
  //   10 Address Bits
  //   (1024 Addresses)
  //   Lower 8 Address Bits
endmodule

module RAM_1KB_with_controller_B (
  input  [31:0] address,
  input  [31:0] data_in,
  input  clock,
  input  [2:0] operation,
  output [1:0] error,
  output [31:0] data_out
);

  wire ram_controller_32bit_1_ram_clock;
  wire [7:0] bitselector_1_out;
  wire [31:0] ram_1kb_b_1_data_out, ram_controller_32bit_1_ram_address, ram_controller_32bit_1_ram_data_out;

  RAM_Controller_32bit ram_controller_32bit_1 (
    .operation(operation), .ram_clock(ram_controller_32bit_1_ram_clock), .data_in(data_in),
    .data_out(data_out), .clock(clock), .address_in(address), .ram_data_in(ram_1kb_b_1_data_out),
    .ram_size(5'b01010), .ram_address(ram_controller_32bit_1_ram_address),
    .ram_data_out(ram_controller_32bit_1_ram_data_out), .error(error));
  BitSelector #(.width(32), .group(8)) bitselector_1 (
    .in(ram_controller_32bit_1_ram_address), .out(bitselector_1_out), .sel(2'b00));
  RAM_1KB_B ram_1kb_b_1 (
    .data_out(ram_1kb_b_1_data_out), .clock(ram_controller_32bit_1_ram_clock),
    .data_in(ram_controller_32bit_1_ram_data_out), .address(bitselector_1_out));

  // Notes on the sheet:
  //   1KB RAM Module With Controller (Instance B)
  //   Data is read on address change.
  //   Data is written on falling clock edge.
  //   10 Address Bits
  //   (1024 Addresses)
  //   Lower 8 Address Bits
endmodule

module InstructionSplitter (
  input  [31:0] instruction,
  output [4:0] opcode,
  output [2:0] func,
  output [3:0] r1,
  output [3:0] r2,
  output [15:0] imm
);


  assign func = instruction[7:5];
  assign imm = instruction[31:16];
  assign opcode = instruction[4:0];
  assign r1 = instruction[11:8];
  assign r2 = instruction[15:12];

  // Notes on the sheet:
  //   Instruction Decoder
  //   5-bit opcode
  //   3-bit function
  //   4-bit register
  //   4-bit register
  //   16-bit immediate
endmodule

module Add4 (
  input  [15:0] d_in,
  output [15:0] d_out
);

  Adder #(.width(16)) adder_1 (.a(d_in), .b(16'h4), .out(d_out));  // open: cin, cout

  // Notes on the sheet:
  //   Adds 4 to the given 16-bit value
endmodule

module ChooseOperandSource (
  input  [15:0] r1,
  input  [15:0] r2,
  input  [15:0] imm,
  input  source,
  output [15:0] A,
  output [15:0] B
);

  Multiplexer #(.width(16), .enable("false")) multiplexer_1 (.in0(r1), .in1(r2), .out(A), .sel(source));
  Multiplexer #(.width(16), .enable("false")) multiplexer_2 (.in0(r2), .in1(imm), .out(B), .sel(source));

  // Notes on the sheet:
  //   - RR
  //   - RI/RIC
  //   Choose the source of operands A and B.
  //   source:
  //   0x0
  //   0x1
  //   A = r1, B = r2
  //   A = r2, B = imm
endmodule

module StatusRegister_Controller (
  input  update_compare,
  input  compare_in,
  input  [15:0] status_old,
  input  [3:0] alu_status_in,
  input  [1:0] error_in,
  input  update_alu,
  output compare_out,
  output [15:0] status_new
);

  wire not_1_out;

  not not_1 (not_1_out, update_compare);
  Multiplexer #(.enable("false")) multiplexer_1 (
    .in0(compare_in), .in1(status_old[0]), .out(status_new[0]), .sel(not_1_out));
  Multiplexer #(.width(4), .enable("false")) multiplexer_2 (
    .in0(status_old[4:1]), .in1(alu_status_in), .out(status_new[4:1]), .sel(update_alu));

  assign compare_out = status_old[0];
  assign status_new[15:5] = {{7{1'b0}}, error_in, 2'b00};

  // Notes on the sheet:
  //   Controller for updating and extracting status register info.
endmodule

module CPU_Controller (
  input  [2:0] PCFunction,
  input  [4:0] PCOpcode,
  input  [1:0] MErrorInstruction,
  input  [1:0] MErrorData,
  input  ClockIn,
  input  [15:0] StatusOld,
  input  Compare,
  input  [3:0] StatusALU,
  output [2:0] OpALU,
  output [2:0] OpShifter,
  output [2:0] OpComparator,
  output [2:0] OpMemory,
  output RegisterWrite,
  output Halt,
  output ClockOut,
  output CalculationSource,
  output RegWriteSource,
  output OperandSource,
  output [15:0] StatusNew,
  output MemAddrSource
);

  wire and_2_out, decoder_1_out0, decoder_1_out1, decoder_1_out2, decoder_1_out3, decoder_1_out4,
       decoder_1_out5, decoder_1_out6, decoder_1_out31, E_ANY, E_OOR, E_UNALIGN, LastCompare, not_1_out,
       T_RR, UseALU, UseComparator, WriteMem;
  wire [1:0] priority_encoder_1_out;

  Multiplexer #(.width(3), .enable("false")) multiplexer_1 (
    .in0(3'b000), .in1(PCFunction), .out(OpShifter), .sel(CalculationSource));
  Multiplexer #(.width(3), .enable("false")) multiplexer_2 (
    .in0(3'b000), .in1(PCFunction), .out(OpComparator), .sel(UseComparator));
  Multiplexer #(.width(3), .enable("false")) multiplexer_3 (
    .in0(3'b000), .in1(PCFunction), .out(OpMemory), .sel(MemAddrSource));
  and and_1 (ClockOut, ClockIn, not_1_out);
  or or_1 (E_OOR, MErrorInstruction[0], MErrorData[0]);
  or or_2 (E_UNALIGN, MErrorData[1], MErrorInstruction[1]);
  not not_1 (not_1_out, Halt);
  Multiplexer #(.select(2), .width(3), .enable("false")) multiplexer_4 (
    .in0(PCFunction), .in1(3'b000), .in2(3'b111), .in3(3'b110), .out(OpALU), .sel(priority_encoder_1_out));
  // Probe on priority_encoder_1_out
  Priority_Encoder #(.select(2)) priority_encoder_1 (
    .in0(1'b1), .in1(CalculationSource), .in2(UseComparator), .in3(MemAddrSource),
    .out(priority_encoder_1_out));
  or or_3 (E_ANY, E_OOR, E_UNALIGN);
  or or_4 (Halt, E_ANY, decoder_1_out31);
  StatusRegister_Controller statusregister_controller_1 (
    .compare_out(LastCompare), .status_old(StatusOld), .update_alu(UseALU), .alu_status_in(StatusALU),
    .error_in({E_UNALIGN, E_OOR}), .compare_in(Compare), .update_compare(UseComparator),
    .status_new(StatusNew));
  and and_2 (and_2_out, decoder_1_out2, LastCompare);
  or or_5 (RegisterWrite, and_2_out, decoder_1_out0, decoder_1_out1, decoder_1_out3, decoder_1_out4, RegWriteSource);
  or or_6 (UseComparator, decoder_1_out5, decoder_1_out6);
  or or_7 (UseALU, UseComparator, decoder_1_out0, decoder_1_out1, MemAddrSource);
  or or_8 (MemAddrSource, RegWriteSource, WriteMem);
  or or_9 (CalculationSource, decoder_1_out3, decoder_1_out4);
  or or_10 (T_RR, decoder_1_out0, decoder_1_out3, decoder_1_out5);
  or or_11 (OperandSource, decoder_1_out1, decoder_1_out2, decoder_1_out4, decoder_1_out6, RegWriteSource, WriteMem);
  Decoder #(.select(5)) decoder_1 (
    .out0(decoder_1_out0), .out1(decoder_1_out1), .out2(decoder_1_out2), .out3(decoder_1_out3),
    .out4(decoder_1_out4), .out5(decoder_1_out5), .out6(decoder_1_out6), .out7(RegWriteSource),
    .out8(WriteMem), .out31(decoder_1_out31), .sel(PCOpcode));  // open: out9, out10, out11, out12, out13, out14, out15, out16, out17, out18, out19, out20, out21, out22, out23, out24, out25, out26, out27, out28, out29, out30, en

  // Other names for the same wires on the sheet: ReadMem = RegWriteSource; T_RI = OperandSource;
  //   UseMemory = MemAddrSource; UseShifter = CalculationSource; WriteReg = RegisterWrite

  // Notes on the sheet:
  //   CPU Control Unit & Instruction Decoder
  //   Operation
  //   Error
  //   Clock
  //   Routing
  //   0 = ALU
  //   1 = Shifter
  //   0 = RR Type
  //   0 = Calculation Result
  //   1 = Memory Read
  //   1 = RI/RIC Type
  //   0 = Zero / Null Address
  //   1 = Calculation Result
  //   Halt
  //   Choose ALU Function
  //   Source
  //   N/A
  //   Sub
  //   Add
  //   Instruction Function
  //   Halt
  //   Status
  //   Register Usage
  //   Memory Usage
  //   Decode
  //   Datapath Usage
  //   Instruction Type
  //   0 - ALU RR
  //   1 - ALU RI
  //   2 - ALU RI(C)
  //   3 - Shifter RR
  //   4 - Shifter RI
  //   5 - Comparator RR
  //   6 - Comparator RI
  //   7 - Memory Load
  //   8 - Memory Store
  //   31 - Halt
  //   Instruction
endmodule

module CPU (
  input  [31:0] dm_data_read,
  input  [31:0] im_data_read,
  input  [1:0] dm_error,
  input  [1:0] im_error,
  input  clock,
  output [31:0] dm_data_write,
  output [31:0] im_data_write,
  output [2:0] im_operation,
  output [31:0] dm_address,
  output [31:0] im_address,
  output [2:0] dm_operation,
  output halt
);

  wire clk, comparator_16bit_1_compare, cpu_controller_1_calculationsource, cpu_controller_1_memaddrsource,
       cpu_controller_1_operandsource, cpu_controller_1_regwritesource, RegWrite;
  wire [2:0] instructionsplitter_1_func, OpALU, OpCompare, OpShift;
  wire [3:0] alu_16bit_extended_1_status, bitselector_1_out, instructionsplitter_1_r1,
       instructionsplitter_1_r2;
  wire [4:0] instructionsplitter_1_opcode;
  wire [15:0] add4_1_d_out, alu_16bit_extended_1_result, bitselector_2_out, chooseoperandsource_1_a,
       chooseoperandsource_1_b, cpu_controller_1_statusnew, instructionsplitter_1_imm, multiplexer_1_out,
       multiplexer_2_out, multiplexer_3_out, register_file_16_1_a_out, register_file_16_1_b_out,
       register_file_16_1_pc_out, register_file_16_1_status_out, shifter_16bit_byn_1_data_out;

  CPU_Controller cpu_controller_1 (
    .OpALU(OpALU), .MErrorInstruction(im_error), .StatusALU(alu_16bit_extended_1_status), .Halt(halt),
    .OpShifter(OpShift), .MErrorData(dm_error), .Compare(comparator_16bit_1_compare),
    .RegisterWrite(RegWrite), .OpComparator(OpCompare), .ClockIn(clock),
    .StatusOld(register_file_16_1_status_out), .OpMemory(dm_operation),
    .PCOpcode(instructionsplitter_1_opcode), .PCFunction(instructionsplitter_1_func), .ClockOut(clk),
    .CalculationSource(cpu_controller_1_calculationsource), .RegWriteSource(cpu_controller_1_regwritesource),
    .OperandSource(cpu_controller_1_operandsource), .StatusNew(cpu_controller_1_statusnew),
    .MemAddrSource(cpu_controller_1_memaddrsource));
  assign im_address = {{16{1'b0}}, register_file_16_1_pc_out};  // Bit_Extender bit_extender_1
  // Probe on im_error
  // Probe on im_data_read
  // Probe on register_file_16_1_pc_out
  InstructionSplitter instructionsplitter_1 (
    .r2(instructionsplitter_1_r2), .r1(instructionsplitter_1_r1), .func(instructionsplitter_1_func),
    .opcode(instructionsplitter_1_opcode), .instruction(im_data_read), .imm(instructionsplitter_1_imm));
  // Probe on instructionsplitter_1_opcode
  // Probe on instructionsplitter_1_func
  // Probe on instructionsplitter_1_r1
  // Probe on instructionsplitter_1_r2
  // Probe on cpu_controller_1_statusnew
  Register_File_16 register_file_16_1 (
    .B_out(register_file_16_1_b_out), .clock(clk), .PC_in(add4_1_d_out),
    .Status_in(cpu_controller_1_statusnew), .write_a(RegWrite), .A_out(register_file_16_1_a_out),
    .A_in(multiplexer_1_out), .A_index(instructionsplitter_1_r1), .B_index(instructionsplitter_1_r2),
    .PC_out(register_file_16_1_pc_out), .Status_out(register_file_16_1_status_out));
  Add4 add4_1 (.d_out(add4_1_d_out), .d_in(register_file_16_1_pc_out));
  // Probe on RegWrite
  // Probe on register_file_16_1_status_out
  // Probe on register_file_16_1_a_out
  // Probe on register_file_16_1_b_out
  // Probe on instructionsplitter_1_imm
  // Probe on cpu_controller_1_operandsource
  ChooseOperandSource chooseoperandsource_1 (
    .A(chooseoperandsource_1_a), .source(cpu_controller_1_operandsource), .imm(instructionsplitter_1_imm),
    .r2(register_file_16_1_b_out), .r1(register_file_16_1_a_out), .B(chooseoperandsource_1_b));
  // Probe on chooseoperandsource_1_a
  // Probe on chooseoperandsource_1_b
  // Probe on OpShift
  ALU_16bit_extended alu_16bit_extended_1 (
    .b(chooseoperandsource_1_b), .a(chooseoperandsource_1_a), .operation(OpALU),
    .result(alu_16bit_extended_1_result), .status(alu_16bit_extended_1_status));
  BitSelector #(.width(16), .group(4)) bitselector_1 (
    .in(chooseoperandsource_1_b), .out(bitselector_1_out), .sel(2'b00));
  Shifter_16bit_byn shifter_16bit_byn_1 (
    .shamt(bitselector_1_out), .data_out(shifter_16bit_byn_1_data_out), .data_in(chooseoperandsource_1_a),
    .operation(OpShift));
  // Probe on OpALU
  // Probe on OpCompare
  Comparator_16bit comparator_16bit_1 (
    .compare(comparator_16bit_1_compare), .status(alu_16bit_extended_1_status), .B(chooseoperandsource_1_b),
    .operation(OpCompare), .A(chooseoperandsource_1_a));
  // Probe on alu_16bit_extended_1_status
  // Probe on comparator_16bit_1_compare
  // Probe on alu_16bit_extended_1_result
  // Probe on shifter_16bit_byn_1_data_out
  // Probe on multiplexer_1_out
  Multiplexer #(.width(16), .enable("false")) multiplexer_1 (
    .in0(multiplexer_2_out), .in1(bitselector_2_out), .out(multiplexer_1_out),
    .sel(cpu_controller_1_regwritesource));
  // Probe on multiplexer_2_out
  Multiplexer #(.width(16), .enable("false")) multiplexer_2 (
    .in0(alu_16bit_extended_1_result), .in1(shifter_16bit_byn_1_data_out), .out(multiplexer_2_out),
    .sel(cpu_controller_1_calculationsource));
  // Probe on cpu_controller_1_calculationsource
  // Probe on register_file_16_1_a_out
  Multiplexer #(.width(16), .enable("false")) multiplexer_3 (
    .in0({16{1'b0}}), .in1(multiplexer_2_out), .out(multiplexer_3_out), .sel(cpu_controller_1_memaddrsource));
  // Probe on cpu_controller_1_regwritesource
  assign dm_data_write = {{16{1'b0}}, register_file_16_1_a_out};  // Bit_Extender bit_extender_2
  BitSelector #(.width(32), .group(16)) bitselector_2 (.in(dm_data_read), .out(bitselector_2_out), .sel(1'b0));
  assign dm_address = {{16{1'b0}}, multiplexer_3_out};  // Bit_Extender bit_extender_3
  // Probe on dm_operation
  // Probe on dm_error

  assign im_data_write = {32{1'b0}};
  assign im_operation = 3'b000;

  // Notes on the sheet:
  //   Custom 16-bit CPU
  //   1 - Fetch
  //   Fetch instruction from memory.
  //   Instruction Access Error
  //   read32
  //   Current Instruction
  //   Instruction Address
  //   Opcode
  //   2 - Extract
  //   Extract instruction fields.
  //   Function
  //   r1 Index
  //   r2 Index
  //   Instruction Address
  //   16-bit immediate
  //   New Status
  //   7 - Write Register
  //   4 - Read Register
  //   Read operand values from registers.
  //   Register Write
  //   r1 Write Value
  //   r1 Read Value
  //   Old Status
  //   r1 Value
  //   r2 Value
  //   16-bit immediate
  //   Choose
  //   Operand
  //   Source
  //   Is RR or RI/RIC ?
  //   Operand Source
  //   A
  //   B
  //   Lower 4 bits
  //   5 - Perform Calculation
  //   Compare, ALU, and Shift simultaneously.
  //   ALU Status
  //   compare
  //   Write
  //   ALU Result
  //   Shift Result
  //   Value To Write
  //   To Register
  //   Choose
  //   Register
  //   Value
  //   Calculation
  //   Result
  //   Choose
  //   Calculation
  //   Result
  //   Mux
  //   Calculation
  //   Result
  //   Value To Write
  //   To Memory
  //   Mux
  //   Register
  //   Write Value
  //   Value Read
  //   From Memory
  //   Memory
  //   Read/Write
  //   Address
  //   Lower 16 bits
  //   Memory Operation
  //   6 - Read/Write Memory
  //   Memory Access Error
endmodule

module InstructionMemory (
  input  [31:0] address,
  input  [31:0] data_write,
  input  [2:0] operation,
  input  clock,
  output [31:0] data_read,
  output [1:0] error
);

  RAM_1KB_with_controller_A ram_1kb_with_controller_a_1 (
    .error(error), .operation(operation), .clock(clock), .data_in(data_write), .address(address),
    .data_out(data_read));

  // Notes on the sheet:
  //   Instruction Memory
endmodule

module DataMemory (
  input  [31:0] address,
  input  [31:0] data_write,
  input  [2:0] operation,
  input  clock,
  output [31:0] data_read,
  output [1:0] error
);

  RAM_1KB_with_controller_B ram_1kb_with_controller_b_1 (
    .error(error), .operation(operation), .clock(clock), .data_in(data_write), .address(address),
    .data_out(data_read));

  // Notes on the sheet:
  //   Data Memory
endmodule

module Computer (
);

  wire and_1_out, clock_1_out, cpu_1_halt, keyboard_1_avail, undriven_2, undriven_3, undriven_4;
  wire [1:0] datamemory_1_error, instructionmemory_1_error;
  wire [2:0] cpu_1_dm_operation, cpu_1_im_operation;
  wire [6:0] keyboard_1_data, undriven;
  wire [31:0] cpu_1_dm_address, cpu_1_dm_data_write, cpu_1_im_address, cpu_1_im_data_write,
       datamemory_1_data_read, instructionmemory_1_data_read;

  and and_1 (and_1_out, clock_1_out, ~cpu_1_halt);  // AND_Gate
  Clock clock_1 (.out(clock_1_out));
  CPU cpu_1 (
    .im_address(cpu_1_im_address), .im_data_write(cpu_1_im_data_write), .im_operation(cpu_1_im_operation),
    .im_data_read(instructionmemory_1_data_read), .im_error(instructionmemory_1_error),
    .dm_address(cpu_1_dm_address), .dm_data_write(cpu_1_dm_data_write), .dm_operation(cpu_1_dm_operation),
    .dm_data_read(datamemory_1_data_read), .dm_error(datamemory_1_error), .clock(and_1_out), .halt(cpu_1_halt));
  LED led_1 (.in(cpu_1_halt));
  InstructionMemory instructionmemory_1 (
    .address(cpu_1_im_address), .clock(and_1_out), .error(instructionmemory_1_error),
    .data_read(instructionmemory_1_data_read), .operation(cpu_1_im_operation),
    .data_write(cpu_1_im_data_write));
  DataMemory datamemory_1 (
    .operation(cpu_1_dm_operation), .error(datamemory_1_error), .address(cpu_1_dm_address),
    .clock(and_1_out), .data_read(datamemory_1_data_read), .data_write(cpu_1_dm_data_write));
  TTY #(.trigger("falling")) tty_1 (.data(undriven), .clk(undriven_2), .clr(undriven_3));  // open: we
  Keyboard #(.trigger("falling")) keyboard_1 (
    .clk(undriven_4), .avail(keyboard_1_avail), .data(keyboard_1_data));  // open: re, clr

  // Notes on the sheet:
  //   16-bit Computer
  //   HALT
  //   System Clock
  //   MMU
  //   I/O
  //   Controller
  //   TTY Controller
  //   Keyboard Controller
endmodule
